// Logisim project BFISA_2.circ as structural Verilog: 3 circuits, main circuit main
module main (
  input  Clk,
  input  Reset,
  input  Input_Valid,
  input  [7:0] Key
);

  wire and_1_out, and_2_out, and_3_out, and_4_out, and_5_out, Cont_inst_hold, Cont_inst_jump,
       Cont_inst_loopback, Cont_inst_memsrc, Cont_inst_modmem, Cont_inst_modptr, Cont_inst_outp,
       debouncer_1_pulse, nor_1_out, nor_2_out, nor_3_out, nor_4_out, not_1_out, not_2_out, not_3_out,
       not_4_out, not_5_out, or_1_out, xor_1_out;
  wire [2:0] rom_1_data;
  wire [6:0] ram_1_data;
  wire [7:0] adder_3_out, multiplexer_5_out, register_1_q;
  wire [7:7] Cont_inst_memop, ram_1_data_2;
  wire [15:0] adder_1_out, adder_2_out, bit_extender_1_out, multiplexer_1_out, multiplexer_2_out,
       multiplexer_3_out, multiplexer_4_out, PC_q, Pointer_q;
  wire [15:3] rom_1_data_2;
  wire [15:15] Cont_inst_ptrop;

  not not_1 (not_1_out, Cont_inst_ptrop[15]);
  Multiplexer #(.enable("false"), .width(16)) multiplexer_1 (
    .in0(Pointer_q), .in1(adder_1_out), .out(multiplexer_1_out), .sel(Cont_inst_modptr));
  Adder #(.width(16)) adder_1 (
    .a({16{Cont_inst_ptrop[15]}}), .b(Pointer_q), .out(adder_1_out), .cin(not_1_out));  // open: cout
  Adder #(.width(16)) adder_2 (.a(PC_q), .b({16{1'b0}}), .out(adder_2_out), .cin(1'b1));  // open: cout
  Multiplexer #(.enable("false"), .width(16)) multiplexer_2 (
    .in0(adder_2_out), .in1(bit_extender_1_out), .out(multiplexer_2_out), .sel(and_1_out));
  and and_1 (and_1_out, xor_1_out, Cont_inst_jump);
  xor xor_1 (xor_1_out, Cont_inst_loopback, and_5_out);
  Debouncer debouncer_1 (.Pulse(debouncer_1_pulse), .Buttn(Input_Valid), .Clk(Clk), .Rst(Reset));
  Decode Cont_inst (
    .Opcode(rom_1_data), .PtrOp(Cont_inst_ptrop[15]), .MemOp(Cont_inst_memop[7]),
    .LoopBack(Cont_inst_loopback), .MemSrc(Cont_inst_memsrc), .ModPtr(Cont_inst_modptr),
    .Jump(Cont_inst_jump), .Outp(Cont_inst_outp), .ModMem(Cont_inst_modmem), .Hold(Cont_inst_hold));
  Register #(.width(16)) Pointer (.D(multiplexer_1_out), .en(1'b1), .clk(not_3_out), .Q(Pointer_q), .clr(Reset));
  Multiplexer #(.enable("false"), .width(16)) multiplexer_3 (
    .in0(PC_q), .in1(multiplexer_2_out), .out(multiplexer_3_out), .sel(or_1_out));
  or or_1 (or_1_out, debouncer_1_pulse, not_2_out);
  not not_2 (not_2_out, Cont_inst_hold);
  Register #(.width(16)) PC (.D(multiplexer_3_out), .en(1'b1), .clk(Clk), .Q(PC_q), .clr(Reset));
  not not_3 (not_3_out, Clk);
  Multiplexer #(.enable("false"), .width(16)) multiplexer_4 (
    .in0(multiplexer_1_out), .in1(Pointer_q), .out(multiplexer_4_out), .sel(not_3_out));
  and and_2 (and_2_out, Cont_inst_modmem, not_3_out);
  ROM #(.addrWidth(16), .dataWidth(16)) rom_1 (.addr(PC_q), .data({rom_1_data_2, rom_1_data}));
  RAM #(.addrWidth(16), .databus("bidir"), .trigger("high")) ram_1 (
    .addr(multiplexer_4_out), .we(and_2_out), .oe(not_4_out), .data({ram_1_data_2[7], ram_1_data}));
  not not_4 (not_4_out, and_2_out);
  TTY #(.cols(50), .rows(21)) tty_1 (.data(ram_1_data), .clk(not_3_out), .we(Cont_inst_outp), .clr(Reset));
  assign bit_extender_1_out = {{3{1'b0}}, rom_1_data_2};  // Bit_Extender bit_extender_1
  assign {ram_1_data_2[7], ram_1_data} = and_2_out ? register_1_q : 8'bz;  // Controlled_Buffer controlled_buffer_1
  nor nor_1 (nor_1_out, ram_1_data_2[7], ram_1_data[6]);
  nor nor_2 (nor_2_out, ram_1_data[5], ram_1_data[4]);
  nor nor_3 (nor_3_out, ram_1_data[3], ram_1_data[2]);
  nor nor_4 (nor_4_out, ram_1_data[1], ram_1_data[0]);
  not not_5 (not_5_out, Cont_inst_memop[7]);
  Adder adder_3 (
    .a({ram_1_data_2[7], ram_1_data}), .b({8{Cont_inst_memop[7]}}), .out(adder_3_out), .cin(not_5_out));  // open: cout
  and and_3 (and_3_out, nor_1_out, nor_2_out);
  and and_4 (and_4_out, nor_3_out, nor_4_out);
  Register register_1 (.D(multiplexer_5_out), .en(1'b1), .clk(and_2_out), .Q(register_1_q), .clr(Reset));
  Multiplexer #(.enable("false"), .width(8)) multiplexer_5 (
    .in0(adder_3_out), .in1(Key), .out(multiplexer_5_out), .sel(Cont_inst_memsrc));
  and and_5 (and_5_out, and_3_out, and_4_out);

  // Notes on the sheet:
  //   contents of rom_1 (hex, n*v repeats v):
  //   8*2 18c 0 4*2 114 0 2 2 0 2 2 2 0 2 2 2 0 2 4*1 3 75 0 2 0 3 0 2 0 0 2 174 1 15d 1 3 45 0 0 6 0 0 3
  //   3 3 6 7*2 6 6 2 2 2 6 0 6 1 1 3 6 0 6 2 2 2 6 6*3 6 8*3 6 0 2 6 0 2 2 6 ffff
endmodule

module Decode (
  input  [2:0] Opcode,
  output PtrOp,
  output MemOp,
  output LoopBack,
  output MemSrc,
  output ModPtr,
  output Jump,
  output Outp,
  output ModMem,
  output Hold
);

  wire and_1_out, and_2_out, nor_3_out, nor_4_out, not_1_out;

  not not_1 (not_1_out, Opcode[2]);
  nor nor_1 (ModPtr, Opcode[1], Opcode[2]);
  nor nor_2 (Jump, Opcode[1], not_1_out);
  nor nor_3 (nor_3_out, Opcode[0], not_1_out);
  and and_1 (and_1_out, Opcode[1], not_1_out);
  and and_2 (and_2_out, Opcode[0], Opcode[1]);
  and and_3 (Outp, nor_3_out, Opcode[1]);
  nor nor_4 (nor_4_out, and_1_out, and_2_out);
  not not_2 (ModMem, nor_4_out);
  and and_4 (Hold, and_2_out, Opcode[2]);

  assign LoopBack = Opcode[0];
  assign MemOp = Opcode[0];
  assign MemSrc = Opcode[2];
  assign PtrOp = Opcode[0];

  // Notes on the sheet:
  //   15 ns
  //   27 ns
  //   22 ns
  //   0
  //   0
  //   0
  //   0
  //   15
  //   37
  //   64
  //   86
  //   54
endmodule

module Debouncer (
  input  Buttn,
  input  Clk,
  input  Rst,
  output Pulse
);

  wire d_ff_1_q, d_ff_2_q, d_ff_3_q, d_ff_4_q, d_ff_5_q, d_ff_6_q, d_ff_7_q, d_ff_8_q, nand_1_out,
       nand_2_out, nor_1_out;

  D_Flip_Flop d_ff_1 (.D(Buttn), .clk(Clk), .Q(d_ff_1_q), .reset(Rst));  // open: Qn, preset
  D_Flip_Flop d_ff_2 (.D(d_ff_1_q), .clk(Clk), .Q(d_ff_2_q), .reset(Rst));  // open: Qn, preset
  D_Flip_Flop d_ff_3 (.D(d_ff_2_q), .clk(Clk), .Q(d_ff_3_q), .reset(Rst));  // open: Qn, preset
  D_Flip_Flop d_ff_4 (.D(d_ff_3_q), .clk(Clk), .Q(d_ff_4_q), .reset(Rst));  // open: Qn, preset
  D_Flip_Flop d_ff_5 (.D(d_ff_4_q), .clk(Clk), .Q(d_ff_5_q), .reset(Rst));  // open: Qn, preset
  D_Flip_Flop d_ff_6 (.D(d_ff_5_q), .clk(Clk), .Q(d_ff_6_q), .reset(Rst));  // open: Qn, preset
  D_Flip_Flop d_ff_7 (.D(d_ff_6_q), .clk(Clk), .Q(d_ff_7_q), .reset(Rst));  // open: Qn, preset
  D_Flip_Flop d_ff_8 (.D(d_ff_7_q), .clk(Clk), .Q(d_ff_8_q), .reset(Rst));  // open: Qn, preset
  nor nor_1 (nor_1_out, d_ff_8_q, d_ff_8_q);
  nand nand_1 (nand_1_out, d_ff_7_q, d_ff_6_q, d_ff_5_q, d_ff_4_q);
  nand nand_2 (nand_2_out, d_ff_3_q, d_ff_2_q, d_ff_1_q, nor_1_out);
  nor nor_2 (Pulse, nand_1_out, nand_2_out);
endmodule
