// Logisim project BFISA_BOM.circ as structural Verilog: 2 circuits, main circuit main
module main (
);

  wire button_1_out, button_2_out, KeyIn_pin2, KeyIn_pin5, KeyIn_pin6, KeyIn_pin9, KeyIn_pin12, KeyIn_pin15,
       KeyIn_pin16, KeyIn_pin19, multiplexer_1_out, multiplexer_2_out, multiplexer_3_out, multiplexer_4_out,
       multiplexer_5_out, multiplexer_6_out, multiplexer_7_out, multiplexer_8_out, multiplexer_9_out,
       multiplexer_10_out, multiplexer_11_out, multiplexer_12_out, multiplexer_13_out, multiplexer_14_out,
       multiplexer_15_out, multiplexer_16_out, multiplexer_17_out, multiplexer_18_out, multiplexer_19_out,
       multiplexer_20_out, multiplexer_21_out, multiplexer_22_out, multiplexer_23_out, multiplexer_24_out,
       multiplexer_25_out, multiplexer_26_out, multiplexer_27_out, multiplexer_28_out, multiplexer_29_out,
       multiplexer_30_out, multiplexer_31_out, multiplexer_32_out, multiplexer_33_out, multiplexer_34_out,
       multiplexer_35_out, multiplexer_36_out, multiplexer_37_out, multiplexer_38_out, multiplexer_39_out,
       multiplexer_40_out, multiplexer_41_out, multiplexer_42_out, multiplexer_43_out, multiplexer_44_out,
       multiplexer_45_out, multiplexer_46_out, multiplexer_47_out, multiplexer_48_out, muxes_2_y1,
       muxes_2_y2, muxes_2_y3, muxes_2_y4, muxes_3_y1, muxes_3_y2, muxes_3_y3, muxes_3_y4, n7402_1_pin3,
       n7402_1_pin11, n7402_3_pin3, n7402_3_pin6, n7402_3_pin8, n7402_3_pin11, n7404_1_pin10, n7408_1_pin2,
       n7408_1_pin3, n7408_1_pin8, n7408_1_pin10, n7408_2_pin2, n7408_2_pin3, n7408_2_pin5, n7408_2_pin6,
       n7408_2_pin11, n7408_2_pin13, n7408_3_pin3, n7408_3_pin11, n7420_1_pin6, n7420_1_pin8, n7420_1_pin9,
       n7432_1_pin1, n7432_1_pin2, n7432_1_pin3, n7486_1_pin8, n7486_1_pin9, n74125_1_pin2, n74125_1_pin5,
       n74125_1_pin9, n74125_1_pin12, n74125_2_pin2, n74125_2_pin5, n74125_2_pin9, n74125_2_pin12,
       n74273_1_pin1, n74273_1_pin11, n74273_3_pin11, n74273_5_pin2, n74273_5_pin5, n74273_5_pin6,
       n74273_5_pin9, n74273_5_pin14, n74273_5_pin17, n74273_5_pin18, n74273_5_pin19, n74283_1_pin1,
       n74283_1_pin2, n74283_1_pin3, n74283_1_pin4, n74283_1_pin5, n74283_1_pin10, n74283_1_pin12,
       n74283_1_pin13, n74283_1_pin14, n74283_1_pin15, n74283_2_pin1, n74283_2_pin2, n74283_2_pin4,
       n74283_2_pin7, n74283_2_pin9, n74283_2_pin10, n74283_2_pin13, n74283_2_pin15, n74283_3_pin1,
       n74283_3_pin4, n74283_3_pin9, n74283_3_pin10, n74283_3_pin13, n74283_4_pin1, n74283_4_pin4,
       n74283_4_pin9, n74283_4_pin10, n74283_4_pin13, n74283_5_pin1, n74283_5_pin4, n74283_5_pin10,
       n74283_5_pin13, n74283_6_pin1, n74283_6_pin3, n74283_6_pin4, n74283_6_pin5, n74283_6_pin7,
       n74283_6_pin9, n74283_6_pin10, n74283_6_pin12, n74283_6_pin13, n74283_6_pin14, n74283_7_pin1,
       n74283_7_pin3, n74283_7_pin4, n74283_7_pin5, n74283_7_pin9, n74283_7_pin10, n74283_7_pin12,
       n74283_7_pin13, n74283_7_pin14, n74283_8_pin1, n74283_8_pin3, n74283_8_pin4, n74283_8_pin5,
       n74283_8_pin9, n74283_8_pin10, n74283_8_pin12, n74283_8_pin13, n74283_8_pin14, n74283_9_pin1,
       n74283_9_pin3, n74283_9_pin4, n74283_9_pin5, n74283_9_pin10, n74283_9_pin12, n74283_9_pin13,
       n74283_9_pin14, n74283_10_pin1, n74283_10_pin4, n74283_10_pin9, n74283_10_pin10, n74283_10_pin13,
       n74283_11_pin1, n74283_11_pin4, n74283_11_pin10, n74283_11_pin13;
  wire [7:0] ram_1_data;
  wire [15:0] multiplexer_49_out, n74283_2_pin5, n74283_6_pin2;

  Muxes muxes_1 (
    .I03(n74283_1_pin14), .I01(n74283_1_pin5), .I13(n74283_1_pin13), .I11(n74283_1_pin4),
    .I04(n74283_1_pin12), .I02(n74283_1_pin3), .I12(n74283_1_pin1), .I14(n74283_1_pin10));  // open: Gnd, E_n, Vcc, S, Y1, Y2, Y3, Y4
  _74283 #(.ShowInternalStructure("true")) u_74283_1 (
    .pin1(n74283_1_pin1), .pin2(n74283_1_pin2), .pin3(n74283_1_pin3), .pin4(n74283_1_pin4),
    .pin5(n74283_1_pin5), .pin6(n74283_1_pin2), .pin15(n74283_1_pin15), .pin14(n74283_1_pin14),
    .pin13(n74283_1_pin13), .pin12(n74283_1_pin12), .pin11(n74283_1_pin15), .pin10(n74283_1_pin10));  // open: pin7, pin9
  _74283 #(.ShowInternalStructure("true")) u_74283_2 (
    .pin1(n74283_2_pin1), .pin2(n74283_2_pin2), .pin3(n74283_2_pin5[1]), .pin4(n74283_2_pin4),
    .pin5(n74283_2_pin5[0]), .pin6(n74283_2_pin2), .pin7(n74283_2_pin7), .pin15(n74283_2_pin15),
    .pin14(n74283_2_pin5[2]), .pin13(n74283_2_pin13), .pin12(n74283_2_pin5[3]), .pin11(n74283_2_pin15),
    .pin10(n74283_2_pin10), .pin9(n74283_2_pin9));
  _74283 #(.ShowInternalStructure("true")) u_74283_3 (
    .pin1(n74283_3_pin1), .pin2(n74283_2_pin2), .pin3(n74283_2_pin5[5]), .pin4(n74283_3_pin4),
    .pin5(n74283_2_pin5[4]), .pin6(n74283_2_pin2), .pin7(n74283_2_pin9), .pin15(n74283_2_pin15),
    .pin14(n74283_2_pin5[6]), .pin13(n74283_3_pin13), .pin12(n74283_2_pin5[7]), .pin11(n74283_2_pin15),
    .pin10(n74283_3_pin10), .pin9(n74283_3_pin9));
  _74283 #(.ShowInternalStructure("true")) u_74283_4 (
    .pin1(n74283_4_pin1), .pin2(n74283_2_pin2), .pin3(n74283_2_pin5[9]), .pin4(n74283_4_pin4),
    .pin5(n74283_2_pin5[8]), .pin6(n74283_2_pin2), .pin7(n74283_3_pin9), .pin15(n74283_2_pin15),
    .pin14(n74283_2_pin5[10]), .pin13(n74283_4_pin13), .pin12(n74283_2_pin5[11]), .pin11(n74283_2_pin15),
    .pin10(n74283_4_pin10), .pin9(n74283_4_pin9));
  _74283 #(.ShowInternalStructure("true")) u_74283_5 (
    .pin1(n74283_5_pin1), .pin2(n74283_2_pin2), .pin3(n74283_2_pin5[13]), .pin4(n74283_5_pin4),
    .pin5(n74283_2_pin5[12]), .pin6(n74283_2_pin2), .pin7(n74283_4_pin9), .pin15(n74283_2_pin15),
    .pin14(n74283_2_pin5[14]), .pin13(n74283_5_pin13), .pin12(n74283_2_pin5[15]), .pin11(n74283_2_pin15),
    .pin10(n74283_5_pin10));  // open: pin9
  _74283 #(.ShowInternalStructure("true")) u_74283_6 (
    .pin1(n74283_6_pin1), .pin2(n74283_6_pin2[0]), .pin3(n74283_6_pin3), .pin4(n74283_6_pin4),
    .pin5(n74283_6_pin5), .pin6(n74283_6_pin2[0]), .pin7(n74283_6_pin7), .pin15(n74283_6_pin2[0]),
    .pin14(n74283_6_pin14), .pin13(n74283_6_pin13), .pin12(n74283_6_pin12), .pin11(n74283_6_pin2[0]),
    .pin10(n74283_6_pin10), .pin9(n74283_6_pin9));
  _74283 #(.ShowInternalStructure("true")) u_74283_7 (
    .pin1(n74283_7_pin1), .pin2(n74283_6_pin2[0]), .pin3(n74283_7_pin3), .pin4(n74283_7_pin4),
    .pin5(n74283_7_pin5), .pin6(n74283_6_pin2[0]), .pin7(n74283_6_pin9), .pin15(n74283_6_pin2[0]),
    .pin14(n74283_7_pin14), .pin13(n74283_7_pin13), .pin12(n74283_7_pin12), .pin11(n74283_6_pin2[0]),
    .pin10(n74283_7_pin10), .pin9(n74283_7_pin9));
  _74283 #(.ShowInternalStructure("true")) u_74283_8 (
    .pin1(n74283_8_pin1), .pin2(n74283_6_pin2[0]), .pin3(n74283_8_pin3), .pin4(n74283_8_pin4),
    .pin5(n74283_8_pin5), .pin6(n74283_6_pin2[0]), .pin7(n74283_7_pin9), .pin15(n74283_6_pin2[0]),
    .pin14(n74283_8_pin14), .pin13(n74283_8_pin13), .pin12(n74283_8_pin12), .pin11(n74283_6_pin2[0]),
    .pin10(n74283_8_pin10), .pin9(n74283_8_pin9));
  _74283 #(.ShowInternalStructure("true")) u_74283_9 (
    .pin1(n74283_9_pin1), .pin2(n74283_6_pin2[0]), .pin3(n74283_9_pin3), .pin4(n74283_9_pin4),
    .pin5(n74283_9_pin5), .pin6(n74283_6_pin2[0]), .pin7(n74283_8_pin9), .pin15(n74283_6_pin2[0]),
    .pin14(n74283_9_pin14), .pin13(n74283_9_pin13), .pin12(n74283_9_pin12), .pin11(n74283_6_pin2[0]),
    .pin10(n74283_9_pin10));  // open: pin9
  Multiplexer #(.enable("false")) multiplexer_1 (
    .in0(n74283_2_pin4), .in1(n74283_6_pin2[3]), .out(multiplexer_1_out), .sel(n7408_1_pin3));
  Multiplexer #(.enable("false")) multiplexer_2 (
    .in0(n74283_2_pin1), .in1(n74283_6_pin2[4]), .out(multiplexer_2_out), .sel(n7408_1_pin3));
  Multiplexer #(.enable("false")) multiplexer_3 (
    .in0(n74283_2_pin13), .in1(n74283_6_pin2[5]), .out(multiplexer_3_out), .sel(n7408_1_pin3));
  Multiplexer #(.enable("false")) multiplexer_4 (
    .in0(n74283_2_pin10), .in1(n74283_6_pin2[6]), .out(multiplexer_4_out), .sel(n7408_1_pin3));
  Multiplexer #(.enable("false")) multiplexer_5 (
    .in0(n74283_3_pin4), .in1(n74283_6_pin2[7]), .out(multiplexer_5_out), .sel(n7408_1_pin3));
  Multiplexer #(.enable("false")) multiplexer_6 (
    .in0(n74283_3_pin1), .in1(n74283_6_pin2[8]), .out(multiplexer_6_out), .sel(n7408_1_pin3));
  Multiplexer #(.enable("false")) multiplexer_7 (
    .in0(n74283_3_pin13), .in1(n74283_6_pin2[9]), .out(multiplexer_7_out), .sel(n7408_1_pin3));
  Multiplexer #(.enable("false")) multiplexer_8 (
    .in0(n74283_3_pin10), .in1(n74283_6_pin2[10]), .out(multiplexer_8_out), .sel(n7408_1_pin3));
  Multiplexer #(.enable("false")) multiplexer_9 (
    .in0(n74283_4_pin4), .in1(n74283_6_pin2[11]), .out(multiplexer_9_out), .sel(n7408_1_pin3));
  Multiplexer #(.enable("false")) multiplexer_10 (
    .in0(n74283_4_pin1), .in1(n74283_6_pin2[12]), .out(multiplexer_10_out), .sel(n7408_1_pin3));
  Multiplexer #(.enable("false")) multiplexer_11 (
    .in0(n74283_4_pin13), .in1(n74283_6_pin2[13]), .out(multiplexer_11_out), .sel(n7408_1_pin3));
  Multiplexer #(.enable("false")) multiplexer_12 (
    .in0(n74283_4_pin10), .in1(n74283_6_pin2[14]), .out(multiplexer_12_out), .sel(n7408_1_pin3));
  Multiplexer #(.enable("false")) multiplexer_13 (
    .in0(n74283_5_pin4), .in1(n74283_6_pin2[15]), .out(multiplexer_13_out), .sel(n7408_1_pin3));
  Multiplexer #(.enable("false")) multiplexer_14 (
    .in0(n74283_5_pin1), .in1(1'b0), .out(multiplexer_14_out), .sel(n7408_1_pin3));
  Multiplexer #(.enable("false")) multiplexer_15 (
    .in0(n74283_5_pin13), .in1(1'b0), .out(multiplexer_15_out), .sel(n7408_1_pin3));
  Multiplexer #(.enable("false")) multiplexer_16 (
    .in0(n74283_5_pin10), .in1(1'b0), .out(multiplexer_16_out), .sel(n7408_1_pin3));
  Multiplexer #(.enable("false")) multiplexer_17 (
    .in0(n74283_6_pin5), .in1(n74283_6_pin4), .out(multiplexer_17_out), .sel(n7402_1_pin11));
  Multiplexer #(.enable("false")) multiplexer_18 (
    .in0(n74283_6_pin3), .in1(n74283_6_pin1), .out(multiplexer_18_out), .sel(n7402_1_pin11));
  Multiplexer #(.enable("false")) multiplexer_19 (
    .in0(n74283_6_pin14), .in1(n74283_6_pin13), .out(multiplexer_19_out), .sel(n7402_1_pin11));
  Multiplexer #(.enable("false")) multiplexer_20 (
    .in0(n74283_6_pin12), .in1(n74283_6_pin10), .out(multiplexer_20_out), .sel(n7402_1_pin11));
  Multiplexer #(.enable("false")) multiplexer_21 (
    .in0(n74283_7_pin5), .in1(n74283_7_pin4), .out(multiplexer_21_out), .sel(n7402_1_pin11));
  Multiplexer #(.enable("false")) multiplexer_22 (
    .in0(n74283_7_pin3), .in1(n74283_7_pin1), .out(multiplexer_22_out), .sel(n7402_1_pin11));
  Multiplexer #(.enable("false")) multiplexer_23 (
    .in0(n74283_7_pin14), .in1(n74283_7_pin13), .out(multiplexer_23_out), .sel(n7402_1_pin11));
  Multiplexer #(.enable("false")) multiplexer_24 (
    .in0(n74283_7_pin12), .in1(n74283_7_pin10), .out(multiplexer_24_out), .sel(n7402_1_pin11));
  Multiplexer #(.enable("false")) multiplexer_25 (
    .in0(n74283_8_pin5), .in1(n74283_8_pin4), .out(multiplexer_25_out), .sel(n7402_1_pin11));
  Multiplexer #(.enable("false")) multiplexer_26 (
    .in0(n74283_8_pin3), .in1(n74283_8_pin1), .out(multiplexer_26_out), .sel(n7402_1_pin11));
  Multiplexer #(.enable("false")) multiplexer_27 (
    .in0(n74283_8_pin14), .in1(n74283_8_pin13), .out(multiplexer_27_out), .sel(n7402_1_pin11));
  Multiplexer #(.enable("false")) multiplexer_28 (
    .in0(n74283_8_pin12), .in1(n74283_8_pin10), .out(multiplexer_28_out), .sel(n7402_1_pin11));
  Multiplexer #(.enable("false")) multiplexer_29 (
    .in0(n74283_9_pin5), .in1(n74283_9_pin4), .out(multiplexer_29_out), .sel(n7402_1_pin11));
  Multiplexer #(.enable("false")) multiplexer_30 (
    .in0(n74283_9_pin3), .in1(n74283_9_pin1), .out(multiplexer_30_out), .sel(n7402_1_pin11));
  Multiplexer #(.enable("false")) multiplexer_31 (
    .in0(n74283_9_pin14), .in1(n74283_9_pin13), .out(multiplexer_31_out), .sel(n7402_1_pin11));
  Multiplexer #(.enable("false")) multiplexer_32 (
    .in0(n74283_9_pin12), .in1(n74283_9_pin10), .out(multiplexer_32_out), .sel(n7402_1_pin11));
  Multiplexer #(.enable("false")) multiplexer_33 (
    .in0(n74283_2_pin5[0]), .in1(multiplexer_1_out), .out(multiplexer_33_out), .sel(n7432_1_pin3));
  Multiplexer #(.enable("false")) multiplexer_34 (
    .in0(n74283_2_pin5[1]), .in1(multiplexer_2_out), .out(multiplexer_34_out), .sel(n7432_1_pin3));
  Multiplexer #(.enable("false")) multiplexer_35 (
    .in0(n74283_2_pin5[2]), .in1(multiplexer_3_out), .out(multiplexer_35_out), .sel(n7432_1_pin3));
  Multiplexer #(.enable("false")) multiplexer_36 (
    .in0(n74283_2_pin5[3]), .in1(multiplexer_4_out), .out(multiplexer_36_out), .sel(n7432_1_pin3));
  Multiplexer #(.enable("false")) multiplexer_37 (
    .in0(n74283_2_pin5[4]), .in1(multiplexer_5_out), .out(multiplexer_37_out), .sel(n7432_1_pin3));
  Multiplexer #(.enable("false")) multiplexer_38 (
    .in0(n74283_2_pin5[5]), .in1(multiplexer_6_out), .out(multiplexer_38_out), .sel(n7432_1_pin3));
  Multiplexer #(.enable("false")) multiplexer_39 (
    .in0(n74283_2_pin5[6]), .in1(multiplexer_7_out), .out(multiplexer_39_out), .sel(n7432_1_pin3));
  Multiplexer #(.enable("false")) multiplexer_40 (
    .in0(n74283_2_pin5[7]), .in1(multiplexer_8_out), .out(multiplexer_40_out), .sel(n7432_1_pin3));
  Multiplexer #(.enable("false")) multiplexer_41 (
    .in0(n74283_2_pin5[8]), .in1(multiplexer_9_out), .out(multiplexer_41_out), .sel(n7432_1_pin3));
  Multiplexer #(.enable("false")) multiplexer_42 (
    .in0(n74283_2_pin5[9]), .in1(multiplexer_10_out), .out(multiplexer_42_out), .sel(n7432_1_pin3));
  Multiplexer #(.enable("false")) multiplexer_43 (
    .in0(n74283_2_pin5[10]), .in1(multiplexer_11_out), .out(multiplexer_43_out), .sel(n7432_1_pin3));
  Multiplexer #(.enable("false")) multiplexer_44 (
    .in0(n74283_2_pin5[11]), .in1(multiplexer_12_out), .out(multiplexer_44_out), .sel(n7432_1_pin3));
  Multiplexer #(.enable("false")) multiplexer_45 (
    .in0(n74283_2_pin5[12]), .in1(multiplexer_13_out), .out(multiplexer_45_out), .sel(n7432_1_pin3));
  Multiplexer #(.enable("false")) multiplexer_46 (
    .in0(n74283_2_pin5[13]), .in1(multiplexer_14_out), .out(multiplexer_46_out), .sel(n7432_1_pin3));
  Multiplexer #(.enable("false")) multiplexer_47 (
    .in0(n74283_2_pin5[14]), .in1(multiplexer_15_out), .out(multiplexer_47_out), .sel(n7432_1_pin3));
  Multiplexer #(.enable("false")) multiplexer_48 (
    .in0(n74283_2_pin5[15]), .in1(multiplexer_16_out), .out(multiplexer_48_out), .sel(n7432_1_pin3));
  _74273 #(.ShowInternalStructure("true")) u_74273_1 (
    .pin1(n74273_1_pin1), .pin2(n74283_6_pin5), .pin3(multiplexer_17_out), .pin4(multiplexer_18_out),
    .pin5(n74283_6_pin3), .pin6(n74283_6_pin14), .pin7(multiplexer_19_out), .pin8(multiplexer_20_out),
    .pin9(n74283_6_pin12), .pin19(n74283_7_pin12), .pin18(multiplexer_24_out), .pin17(multiplexer_23_out),
    .pin16(n74283_7_pin14), .pin15(n74283_7_pin3), .pin14(multiplexer_22_out), .pin13(multiplexer_21_out),
    .pin12(n74283_7_pin5), .pin11(n74273_1_pin11));
  _74273 #(.ShowInternalStructure("true")) u_74273_2 (
    .pin1(n74273_1_pin1), .pin2(n74283_8_pin5), .pin3(multiplexer_25_out), .pin4(multiplexer_26_out),
    .pin5(n74283_8_pin3), .pin6(n74283_8_pin14), .pin7(multiplexer_27_out), .pin8(multiplexer_28_out),
    .pin9(n74283_8_pin12), .pin19(n74283_9_pin12), .pin18(multiplexer_32_out), .pin17(multiplexer_31_out),
    .pin16(n74283_9_pin14), .pin15(n74283_9_pin3), .pin14(multiplexer_30_out), .pin13(multiplexer_29_out),
    .pin12(n74283_9_pin5), .pin11(n74273_1_pin11));
  _74273 #(.ShowInternalStructure("true")) u_74273_3 (
    .pin1(n74273_1_pin1), .pin2(n74283_2_pin5[0]), .pin3(multiplexer_33_out), .pin4(multiplexer_34_out),
    .pin5(n74283_2_pin5[1]), .pin6(n74283_2_pin5[2]), .pin7(multiplexer_35_out), .pin8(multiplexer_36_out),
    .pin9(n74283_2_pin5[3]), .pin19(n74283_2_pin5[7]), .pin18(multiplexer_40_out),
    .pin17(multiplexer_39_out), .pin16(n74283_2_pin5[6]), .pin15(n74283_2_pin5[5]),
    .pin14(multiplexer_38_out), .pin13(multiplexer_37_out), .pin12(n74283_2_pin5[4]), .pin11(n74273_3_pin11));
  _74273 #(.ShowInternalStructure("true")) u_74273_4 (
    .pin1(n74273_1_pin1), .pin2(n74283_2_pin5[8]), .pin3(multiplexer_41_out), .pin4(multiplexer_42_out),
    .pin5(n74283_2_pin5[9]), .pin6(n74283_2_pin5[10]), .pin7(multiplexer_43_out), .pin8(multiplexer_44_out),
    .pin9(n74283_2_pin5[11]), .pin19(n74283_2_pin5[15]), .pin18(multiplexer_48_out),
    .pin17(multiplexer_47_out), .pin16(n74283_2_pin5[14]), .pin15(n74283_2_pin5[13]),
    .pin14(multiplexer_46_out), .pin13(multiplexer_45_out), .pin12(n74283_2_pin5[12]), .pin11(n74273_3_pin11));
  _7486 #(.ShowInternalStructure("true")) u_7486_1 (
    .pin10(n74283_6_pin2[0]), .pin9(n7486_1_pin9), .pin8(n7486_1_pin8));  // open: pin1, pin2, pin3, pin4, pin5, pin6, pin13, pin12, pin11
  _7408 #(.ShowInternalStructure("true")) u_7408_1 (
    .pin1(n7486_1_pin8), .pin2(n7408_1_pin2), .pin3(n7408_1_pin3), .pin10(n7408_1_pin10),
    .pin9(n74273_1_pin11), .pin8(n7408_1_pin8));  // open: pin4, pin5, pin6, pin13, pin12, pin11
  _7432 #(.ShowInternalStructure("true")) u_7432_1 (
    .pin1(n7432_1_pin1), .pin2(n7432_1_pin2), .pin3(n7432_1_pin3));  // open: pin4, pin5, pin6, pin13, pin12, pin11, pin10, pin9, pin8
  Multiplexer #(.enable("false")) multiplexer_49 (
    .in0(multiplexer_17_out), .in1(n74283_6_pin5), .out(multiplexer_49_out[0]), .sel(n74273_1_pin11));
  Multiplexer #(.enable("false")) multiplexer_50 (
    .in0(multiplexer_18_out), .in1(n74283_6_pin3), .out(multiplexer_49_out[1]), .sel(n74273_1_pin11));
  Multiplexer #(.enable("false")) multiplexer_51 (
    .in0(multiplexer_19_out), .in1(n74283_6_pin14), .out(multiplexer_49_out[2]), .sel(n74273_1_pin11));
  Multiplexer #(.enable("false")) multiplexer_52 (
    .in0(multiplexer_20_out), .in1(n74283_6_pin12), .out(multiplexer_49_out[3]), .sel(n74273_1_pin11));
  Multiplexer #(.enable("false")) multiplexer_53 (
    .in0(multiplexer_21_out), .in1(n74283_7_pin5), .out(multiplexer_49_out[4]), .sel(n74273_1_pin11));
  Multiplexer #(.enable("false")) multiplexer_54 (
    .in0(multiplexer_22_out), .in1(n74283_7_pin3), .out(multiplexer_49_out[5]), .sel(n74273_1_pin11));
  Multiplexer #(.enable("false")) multiplexer_55 (
    .in0(multiplexer_23_out), .in1(n74283_7_pin14), .out(multiplexer_49_out[6]), .sel(n74273_1_pin11));
  Multiplexer #(.enable("false")) multiplexer_56 (
    .in0(multiplexer_24_out), .in1(n74283_7_pin12), .out(multiplexer_49_out[7]), .sel(n74273_1_pin11));
  Multiplexer #(.enable("false")) multiplexer_57 (
    .in0(multiplexer_25_out), .in1(n74283_8_pin5), .out(multiplexer_49_out[8]), .sel(n74273_1_pin11));
  Multiplexer #(.enable("false")) multiplexer_58 (
    .in0(multiplexer_26_out), .in1(n74283_8_pin3), .out(multiplexer_49_out[9]), .sel(n74273_1_pin11));
  Multiplexer #(.enable("false")) multiplexer_59 (
    .in0(multiplexer_27_out), .in1(n74283_8_pin14), .out(multiplexer_49_out[10]), .sel(n74273_1_pin11));
  Multiplexer #(.enable("false")) multiplexer_60 (
    .in0(multiplexer_28_out), .in1(n74283_8_pin12), .out(multiplexer_49_out[11]), .sel(n74273_1_pin11));
  Multiplexer #(.enable("false")) multiplexer_61 (
    .in0(multiplexer_29_out), .in1(n74283_9_pin5), .out(multiplexer_49_out[12]), .sel(n74273_1_pin11));
  Multiplexer #(.enable("false")) multiplexer_62 (
    .in0(multiplexer_30_out), .in1(n74283_9_pin3), .out(multiplexer_49_out[13]), .sel(n74273_1_pin11));
  Multiplexer #(.enable("false")) multiplexer_63 (
    .in0(multiplexer_31_out), .in1(n74283_9_pin14), .out(multiplexer_49_out[14]), .sel(n74273_1_pin11));
  Multiplexer #(.enable("false")) multiplexer_64 (
    .in0(multiplexer_32_out), .in1(n74283_9_pin12), .out(multiplexer_49_out[15]), .sel(n74273_1_pin11));
  ROM #(.addrWidth(16), .dataWidth(16)) rom_1 (.addr(n74283_2_pin5), .data(n74283_6_pin2));
  _7408 #(.ShowInternalStructure("true")) u_7408_2 (
    .pin1(n74283_6_pin2[1]), .pin2(n7408_2_pin2), .pin3(n7408_2_pin3), .pin4(n74283_6_pin2[1]),
    .pin5(n7408_2_pin5), .pin6(n7408_2_pin6), .pin13(n7408_2_pin13), .pin12(n74283_6_pin2[2]),
    .pin11(n7408_2_pin11), .pin10(n74283_6_pin2[0]), .pin9(n74283_6_pin2[1]), .pin8(n7408_2_pin13));
  _7402 #(.ShowInternalStructure("true")) u_7402_1 (
    .pin1(n7408_2_pin13), .pin2(n7408_2_pin6), .pin3(n7402_1_pin3), .pin4(n7408_2_pin5),
    .pin5(n74283_6_pin2[0]), .pin6(n7408_2_pin2), .pin13(n74283_6_pin2[1]), .pin12(n74283_6_pin2[2]),
    .pin11(n7402_1_pin11), .pin10(n74283_6_pin2[1]), .pin9(n7408_2_pin5), .pin8(n7408_1_pin2));
  _7404 #(.ShowInternalStructure("true")) u_7404_1 (
    .pin1(n7402_1_pin3), .pin2(n7408_1_pin10), .pin3(n74283_6_pin2[2]), .pin4(n7408_2_pin5),
    .pin5(n74283_6_pin2[0]), .pin6(n74283_6_pin7), .pin13(n7408_2_pin11), .pin12(n7432_1_pin1),
    .pin11(n7408_1_pin8), .pin10(n7404_1_pin10), .pin9(n74273_3_pin11), .pin8(n74273_1_pin11));
  RAM #(.addrWidth(16), .trigger("high")) ram_1 (
    .addr(multiplexer_49_out), .we(n7408_1_pin8), .oe(n7404_1_pin10), .data(ram_1_data));
  Button button_1 (.out(button_1_out));
  Button button_2 (.out(button_2_out));
  not not_1 (n74273_1_pin1, button_1_out);
  _74273 #(.ShowInternalStructure("true")) u_74273_5 (
    .pin1(n74273_1_pin1), .pin2(n74273_5_pin2), .pin3(button_2_out), .pin4(n74273_5_pin2),
    .pin5(n74273_5_pin5), .pin6(n74273_5_pin6), .pin7(n74273_5_pin5), .pin8(n74273_5_pin6),
    .pin9(n74273_5_pin9), .pin19(n74273_5_pin19), .pin18(n74273_5_pin18), .pin17(n74273_5_pin17),
    .pin16(n74273_5_pin18), .pin15(n74273_5_pin17), .pin14(n74273_5_pin14), .pin13(n74273_5_pin9),
    .pin12(n74273_5_pin14), .pin11(n74273_3_pin11));
  Clock clock_1 (.out(n74273_3_pin11));
  _7420 #(.ShowInternalStructure("true")) u_7420_1 (
    .pin1(n74273_5_pin9), .pin2(n74273_5_pin6), .pin4(n74273_5_pin5), .pin5(n74273_5_pin2),
    .pin6(n7420_1_pin6), .pin13(n74273_5_pin14), .pin12(n74273_5_pin17), .pin10(n74273_5_pin18),
    .pin9(n7420_1_pin9), .pin8(n7420_1_pin8));  // open: pin3, pin11
  _7402 #(.ShowInternalStructure("true")) u_7402_2 (
    .pin1(n7420_1_pin8), .pin2(n7420_1_pin6), .pin3(n7432_1_pin2), .pin13(n74273_5_pin19),
    .pin12(n74273_5_pin19), .pin11(n7420_1_pin9));  // open: pin4, pin5, pin6, pin10, pin9, pin8
  _74125 #(.ShowInternalStructure("true")) u_74125_1 (
    .pin1(n7404_1_pin10), .pin2(n74125_1_pin2), .pin3(ram_1_data[0]), .pin4(n7404_1_pin10),
    .pin5(n74125_1_pin5), .pin6(ram_1_data[1]), .pin13(n7404_1_pin10), .pin12(n74125_1_pin12),
    .pin11(ram_1_data[2]), .pin10(n7404_1_pin10), .pin9(n74125_1_pin9), .pin8(ram_1_data[3]));
  _74125 #(.ShowInternalStructure("true")) u_74125_2 (
    .pin1(n7404_1_pin10), .pin2(n74125_2_pin2), .pin3(ram_1_data[4]), .pin4(n7404_1_pin10),
    .pin5(n74125_2_pin5), .pin6(ram_1_data[5]), .pin13(n7404_1_pin10), .pin12(n74125_2_pin12),
    .pin11(ram_1_data[6]), .pin10(n7404_1_pin10), .pin9(n74125_2_pin9), .pin8(ram_1_data[7]));
  _74283 #(.ShowInternalStructure("true")) u_74283_10 (
    .pin1(n74283_10_pin1), .pin2(n74283_6_pin2[0]), .pin3(ram_1_data[1]), .pin4(n74283_10_pin4),
    .pin5(ram_1_data[0]), .pin6(n74283_6_pin2[0]), .pin7(n74283_6_pin7), .pin15(n74283_6_pin2[0]),
    .pin14(ram_1_data[2]), .pin13(n74283_10_pin13), .pin12(ram_1_data[3]), .pin11(n74283_6_pin2[0]),
    .pin10(n74283_10_pin10), .pin9(n74283_10_pin9));
  _74283 #(.ShowInternalStructure("true")) u_74283_11 (
    .pin1(n74283_11_pin1), .pin2(n74283_6_pin2[0]), .pin3(ram_1_data[5]), .pin4(n74283_11_pin4),
    .pin5(ram_1_data[4]), .pin6(n74283_6_pin2[0]), .pin7(n74283_10_pin9), .pin15(n74283_6_pin2[0]),
    .pin14(ram_1_data[6]), .pin13(n74283_11_pin13), .pin12(ram_1_data[7]), .pin11(n74283_6_pin2[0]),
    .pin10(n74283_11_pin10));  // open: pin9
  TTY #(.rows(32), .cols(64)) tty_1 (
    .data(ram_1_data[6:0]), .clk(n74273_1_pin11), .we(n7408_2_pin3), .clr(button_1_out));
  Muxes muxes_2 (
    .I03(n74283_10_pin13), .I01(n74283_10_pin4), .E_n(1'b0), .I13(KeyIn_pin6), .I11(KeyIn_pin2),
    .S(n74283_6_pin2[2]), .I04(n74283_10_pin10), .I02(n74283_10_pin1), .I12(KeyIn_pin5), .I14(KeyIn_pin9),
    .Y1(muxes_2_y1), .Y2(muxes_2_y2), .Y3(muxes_2_y3), .Y4(muxes_2_y4));  // open: Gnd, Vcc
  Muxes muxes_3 (
    .I03(n74283_11_pin13), .I01(n74283_11_pin4), .E_n(1'b0), .I13(KeyIn_pin16), .I11(KeyIn_pin12),
    .S(n74283_6_pin2[2]), .I04(n74283_11_pin10), .I02(n74283_11_pin1), .I12(KeyIn_pin15), .I14(KeyIn_pin19),
    .Y1(muxes_3_y1), .Y2(muxes_3_y2), .Y3(muxes_3_y3), .Y4(muxes_3_y4));  // open: Gnd, Vcc
  _74273 #(.ShowInternalStructure("true")) ALUReg (
    .pin1(n74273_1_pin1), .pin2(n74125_1_pin2), .pin3(muxes_2_y1), .pin4(muxes_2_y2), .pin5(n74125_1_pin5),
    .pin6(n74125_1_pin12), .pin7(muxes_2_y3), .pin8(muxes_2_y4), .pin9(n74125_1_pin9), .pin19(n74125_2_pin9),
    .pin18(muxes_3_y4), .pin17(muxes_3_y3), .pin16(n74125_2_pin12), .pin15(n74125_2_pin5),
    .pin14(muxes_3_y2), .pin13(muxes_3_y1), .pin12(n74125_2_pin2), .pin11(n7408_1_pin8));
  _74273 #(.ShowInternalStructure("true")) KeyIn (
    .pin2(KeyIn_pin2), .pin5(KeyIn_pin5), .pin6(KeyIn_pin6), .pin9(KeyIn_pin9), .pin19(KeyIn_pin19),
    .pin16(KeyIn_pin16), .pin15(KeyIn_pin15), .pin12(KeyIn_pin12));  // open: pin1, pin3, pin4, pin7, pin8, pin18, pin17, pin14, pin13, pin11
  _7402 #(.ShowInternalStructure("true")) u_7402_3 (
    .pin1(ram_1_data[4]), .pin2(ram_1_data[5]), .pin3(n7402_3_pin3), .pin4(ram_1_data[6]),
    .pin5(ram_1_data[7]), .pin6(n7402_3_pin6), .pin13(ram_1_data[3]), .pin12(ram_1_data[2]),
    .pin11(n7402_3_pin11), .pin10(ram_1_data[1]), .pin9(ram_1_data[0]), .pin8(n7402_3_pin8));
  _7408 #(.ShowInternalStructure("true")) u_7408_3 (
    .pin1(n7402_3_pin6), .pin2(n7402_3_pin3), .pin3(n7408_3_pin3), .pin13(n7402_3_pin8),
    .pin12(n7402_3_pin11), .pin11(n7408_3_pin11), .pin10(n7408_3_pin11), .pin9(n7408_3_pin3),
    .pin8(n7486_1_pin9));  // open: pin4, pin5, pin6
  // also tied to GND on the sheet: {n74283_2_pin2, n74283_2_pin15}
  // also tied to VCC on the sheet: n74283_2_pin7

  // Notes on the sheet:
  //   contents of rom_1 (hex, n*v repeats v):
  //   0 0 0 1 1 1 2 7c 7 0 1 6 0 2 3d ffff 2 2 2 0 10*2 0 2
endmodule

module Muxes (
  input  I01,
  input  I11,
  input  I02,
  input  I12,
  input  Vcc,
  input  Gnd,
  input  I03,
  input  I13,
  input  I04,
  input  I14,
  input  S,
  input  E_n,
  output Y1,
  output Y2,
  output Y3,
  output Y4
);

  wire not_1_out;

  not not_1 (not_1_out, E_n);
  Multiplexer multiplexer_1 (.in0(I01), .in1(I11), .out(Y1), .sel(S), .en(not_1_out));
  Multiplexer multiplexer_2 (.in0(I02), .in1(I12), .out(Y2), .sel(S), .en(not_1_out));
  Multiplexer multiplexer_3 (.in0(I03), .in1(I13), .out(Y3), .sel(S), .en(not_1_out));
  Multiplexer multiplexer_4 (.in0(I04), .in1(I14), .out(Y4), .sel(S), .en(not_1_out));
endmodule
