// Logisim project BFISA_VHDL.circ as structural Verilog: 6 circuits, main circuit main
module main (
  input  [7:0] Key
);

  wire and_1_out, and_2_out, and_3_out, and_4_out, and_5_out, and_6_out, and_7_out, Clk_out, comparator_1_gt,
       comparator_2_eq, d_ff_1_q, d_ff_2_q, dbcr_pulse, decoder_hold, decoder_jump, decoder_loopback,
       decoder_memsrc, decoder_modmem, decoder_modptr, decoder_outp, Input_Valid_out, nand_1_out, nand_2_out,
       nor_1_out, nor_2_out, nor_3_out, nor_4_out, not_1_out, not_2_out, not_3_out, not_4_out, not_5_out,
       or_1_out, or_2_out, Reset_out, xor_1_out;
  wire [2:0] program_data;
  wire [3:0] mem_dout, mem_dout_2, multiplexer_3_out, multiplexer_3_out_2;
  wire [7:0] adder_4_out, multiplexer_2_out;
  wire [7:7] decoder_memop;
  wire [15:0] adder_1_out, adder_2_out, adder_3_out, bit_extender_1_out, counter_1_q, multiplexer_1_out,
       next_ptr_q, PC_q, Pointer_q, register_1_q;
  wire [15:3] program_data_2;
  wire [15:15] decoder_ptrop;

  Clock Clk (.out(Clk_out));
  Button Reset (.out(Reset_out));
  Button Input_Valid (.out(Input_Valid_out));
  not not_1 (not_1_out, decoder_ptrop[15]);
  Comparator #(.width(16)) comparator_1 (.a(Pointer_q), .b(register_1_q), .gt(comparator_1_gt));  // open: eq, lt
  Adder #(.width(16)) adder_1 (
    .a({16{decoder_ptrop[15]}}), .b(Pointer_q), .out(adder_1_out), .cin(not_1_out));  // open: cout
  Register #(.width(16)) register_1 (
    .D(Pointer_q), .en(comparator_1_gt), .clk(Clk_out), .Q(register_1_q), .clr(Reset_out));
  Adder #(.width(16)) adder_2 (.a(PC_q), .b({16{1'b0}}), .out(adder_2_out), .cin(1'b1));  // open: cout
  Multiplexer #(.enable("false"), .width(16)) multiplexer_1 (
    .in0(adder_2_out), .in1(bit_extender_1_out), .out(multiplexer_1_out), .sel(and_1_out));
  and and_1 (and_1_out, xor_1_out, decoder_jump);
  xor xor_1 (xor_1_out, decoder_loopback, and_6_out);
  Debouncer dbcr (.Pulse(dbcr_pulse), .Buttn(Input_Valid_out), .Clk(Clk_out), .Rst(Reset_out));
  Decode decoder (
    .Opcode(program_data), .PtrOp(decoder_ptrop[15]), .MemOp(decoder_memop[7]), .LoopBack(decoder_loopback),
    .MemSrc(decoder_memsrc), .ModPtr(decoder_modptr), .Jump(decoder_jump), .Outp(decoder_outp),
    .ModMem(decoder_modmem), .Hold(decoder_hold));
  Register #(.width(16)) Pointer (.D(adder_1_out), .en(decoder_modptr), .clk(Clk_out), .Q(Pointer_q), .clr(Reset_out));
  or or_1 (or_1_out, dbcr_pulse, not_2_out);
  not not_2 (not_2_out, decoder_hold);
  Hex_Digit_Display hex_digit_display_1 (.value(register_1_q[15:12]));  // open: dp
  Register #(.width(16)) PC (.D(multiplexer_1_out), .en(and_2_out), .clk(Clk_out), .Q(PC_q), .clr(Reset_out));
  and and_2 (and_2_out, or_1_out, and_4_out);
  Hex_Digit_Display hex_digit_display_2 (.value(register_1_q[11:8]));  // open: dp
  Hex_Digit_Display hex_digit_display_3 (.value(register_1_q[7:4]));  // open: dp
  ROM #(.addrWidth(16), .dataWidth(16)) \program  (.addr(PC_q), .data({program_data_2, program_data}));
  D_Flip_Flop d_ff_1 (.D(decoder_modptr), .clk(Clk_out), .Q(d_ff_1_q), .reset(Reset_out));  // open: Qn, preset
  Hex_Digit_Display hex_digit_display_4 (.value(register_1_q[3:0]));  // open: dp
  Adder #(.width(16)) adder_3 (.a(next_ptr_q), .b({16{1'b0}}), .out(adder_3_out), .cin(1'b1));  // open: cout
  Comparator #(.width(16)) comparator_2 (.a(next_ptr_q), .b(Pointer_q), .eq(comparator_2_eq));  // open: gt, lt
  not not_3 (not_3_out, Clk_out);
  nand nand_1 (nand_1_out, d_ff_1_q, decoder_modmem);
  and and_3 (and_3_out, nand_1_out, decoder_modmem);
  Register #(.width(16)) next_ptr (
    .D(adder_3_out), .en(comparator_2_eq), .clk(Clk_out), .Q(next_ptr_q), .clr(Reset_out));
  or or_2 (or_2_out, and_3_out, comparator_2_eq);
  assign bit_extender_1_out = {{3{1'b0}}, program_data_2};  // Bit_Extender bit_extender_1
  D_Flip_Flop d_ff_2 (.D(decoder_outp), .clk(Clk_out), .Q(d_ff_2_q));  // open: Qn, preset, reset
  RAM #(.addrWidth(16)) mem (
    .addr(Pointer_q), .we(or_2_out), .oe(1'b1), .clk(Clk_out), .din(multiplexer_2_out),
    .dout({mem_dout_2, mem_dout}));
  Multiplexer #(.enable("false"), .width(8)) multiplexer_2 (
    .in0({multiplexer_3_out_2, multiplexer_3_out}), .in1({8{1'b0}}), .out(multiplexer_2_out),
    .sel(comparator_2_eq));
  TTY #(.cols(36), .rows(21)) tty_1 (
    .data({mem_dout_2[2:0], mem_dout}), .clk(not_3_out), .we(d_ff_2_q), .clr(Reset_out));
  nand nand_2 (nand_2_out, d_ff_1_q, decoder_jump);
  and and_4 (and_4_out, nand_2_out, nand_1_out);
  not not_4 (not_4_out, decoder_memop[7]);
  Adder adder_4 (
    .a({mem_dout_2, mem_dout}), .b({8{decoder_memop[7]}}), .out(adder_4_out), .cin(not_4_out));  // open: cout
  nor nor_1 (nor_1_out, mem_dout[0], mem_dout[1]);
  nor nor_2 (nor_2_out, mem_dout[2], mem_dout[3]);
  nor nor_3 (nor_3_out, mem_dout_2[0], mem_dout_2[1]);
  nor nor_4 (nor_4_out, mem_dout_2[2], mem_dout_2[3]);
  Multiplexer #(.enable("false"), .width(8)) multiplexer_3 (
    .in0(adder_4_out), .in1(Key), .out({multiplexer_3_out_2, multiplexer_3_out}), .sel(decoder_memsrc));
  and and_5 (and_5_out, nor_1_out, nor_2_out);
  and and_6 (and_6_out, and_5_out, and_7_out);
  and and_7 (and_7_out, nor_3_out, nor_4_out);
  Hex_Digit_Display hex_digit_display_5 (.value(mem_dout_2));  // open: dp
  Hex_Digit_Display hex_digit_display_6 (.value(multiplexer_3_out_2));  // open: dp
  Hex_Digit_Display hex_digit_display_7 (.value(multiplexer_3_out));  // open: dp
  Hex_Digit_Display hex_digit_display_8 (.value(counter_1_q[15:12]));  // open: dp
  Counter #(.max('hffff), .width(16)) counter_1 (
    .clr(Reset_out), .load(1'b0), .up(1'b1), .count(not_5_out), .clk(Clk_out), .Q(counter_1_q));  // open: D, carry
  not not_5 (not_5_out, decoder_hold);
  Hex_Digit_Display hex_digit_display_9 (.value(mem_dout));  // open: dp
  Hex_Digit_Display hex_digit_display_10 (.value(counter_1_q[11:8]));  // open: dp
  Hex_Digit_Display hex_digit_display_11 (.value(counter_1_q[7:4]));  // open: dp
  Hex_Digit_Display hex_digit_display_12 (.value(counter_1_q[3:0]));  // open: dp

  // Notes on the sheet:
  //   contents of program (hex, n*v repeats v):
  //   0 1 8*2 19c 0 4*2 124 0 2 2 0 2 2 2 0 2 2 2 0 2 4*1 3 85 0 2 0 3 0 2 0 0 2 184 1 16d 1 3 55 0 0 6 0
  //   0 3 3 3 6 7*2 6 6 2 2 2 6 0 6 1 1 3 6 0 6 2 2 2 6 6*3 6 8*3 6 0 2 6 0 2 2 6 ffff
endmodule

module Decode (
  input  [2:0] Opcode,
  output PtrOp,
  output MemOp,
  output LoopBack,
  output MemSrc,
  output ModPtr,
  output Jump,
  output Outp,
  output ModMem,
  output Hold
);

  wire and_1_out, and_2_out, nor_3_out, nor_4_out, not_1_out;

  not not_1 (not_1_out, Opcode[2]);
  nor nor_1 (ModPtr, Opcode[1], Opcode[2]);
  nor nor_2 (Jump, Opcode[1], not_1_out);
  nor nor_3 (nor_3_out, Opcode[0], not_1_out);
  and and_1 (and_1_out, Opcode[1], not_1_out);
  and and_2 (and_2_out, Opcode[0], Opcode[1]);
  and and_3 (Outp, nor_3_out, Opcode[1]);
  nor nor_4 (nor_4_out, and_1_out, and_2_out);
  not not_2 (ModMem, nor_4_out);
  and and_4 (Hold, and_2_out, Opcode[2]);

  assign LoopBack = Opcode[0];
  assign MemOp = Opcode[0];
  assign MemSrc = Opcode[2];
  assign PtrOp = Opcode[0];
endmodule

module Debouncer (
  input  Buttn,
  input  Clk,
  input  Rst,
  output Pulse
);

  wire d_ff_1_q, d_ff_2_q, d_ff_3_q, d_ff_4_q, d_ff_5_q, d_ff_6_q, d_ff_7_q, d_ff_8_q, nand_1_out,
       nand_2_out, nor_1_out;

  D_Flip_Flop d_ff_1 (.D(Buttn), .clk(Clk), .Q(d_ff_1_q), .reset(Rst));  // open: Qn, preset
  D_Flip_Flop d_ff_2 (.D(d_ff_1_q), .clk(Clk), .Q(d_ff_2_q), .reset(Rst));  // open: Qn, preset
  D_Flip_Flop d_ff_3 (.D(d_ff_2_q), .clk(Clk), .Q(d_ff_3_q), .reset(Rst));  // open: Qn, preset
  D_Flip_Flop d_ff_4 (.D(d_ff_3_q), .clk(Clk), .Q(d_ff_4_q), .reset(Rst));  // open: Qn, preset
  D_Flip_Flop d_ff_5 (.D(d_ff_4_q), .clk(Clk), .Q(d_ff_5_q), .reset(Rst));  // open: Qn, preset
  D_Flip_Flop d_ff_6 (.D(d_ff_5_q), .clk(Clk), .Q(d_ff_6_q), .reset(Rst));  // open: Qn, preset
  D_Flip_Flop d_ff_7 (.D(d_ff_6_q), .clk(Clk), .Q(d_ff_7_q), .reset(Rst));  // open: Qn, preset
  D_Flip_Flop d_ff_8 (.D(d_ff_7_q), .clk(Clk), .Q(d_ff_8_q), .reset(Rst));  // open: Qn, preset
  nor nor_1 (nor_1_out, d_ff_8_q, d_ff_8_q);
  nand nand_1 (nand_1_out, d_ff_7_q, d_ff_6_q, d_ff_5_q, d_ff_4_q);
  nand nand_2 (nand_2_out, d_ff_3_q, d_ff_2_q, d_ff_1_q, nor_1_out);
  nor nor_2 (Pulse, nand_1_out, nand_2_out);
endmodule

module main_synth (
  input  Clk,
  input  Rst,
  input  Input_valid,
  input  [7:0] Key,
  output [6:0] Char_out,
  output out_enable
);

  wire and_1_out, and_2_out, and_3_out, and_4_out, comparator_1_eq, dbcr_pulse, decoder_hold, decoder_jump,
       decoder_loopback, decoder_memsrc, decoder_modmem, decoder_modptr, nor_1_out, nor_2_out, nor_3_out,
       nor_4_out, not_1_out, not_2_out, not_3_out, not_4_out, or_1_out, or_2_out, xor_1_out;
  wire [2:0] program_data;
  wire [7:0] adder_4_out, multiplexer_3_out, multiplexer_4_out;
  wire [7:7] decoder_memop, mem_dout;
  wire [15:0] adder_1_out, adder_2_out, adder_3_out, bit_extender_1_out, multiplexer_1_out,
       multiplexer_2_out, next_ptr_q, PC_q, Pointer_q;
  wire [15:3] program_data_2;
  wire [15:15] decoder_ptrop;

  not not_1 (not_1_out, decoder_ptrop[15]);
  Adder #(.width(16)) adder_1 (
    .a({16{decoder_ptrop[15]}}), .b(Pointer_q), .out(adder_1_out), .cin(not_1_out));  // open: cout
  Adder #(.width(16)) adder_2 (.a(PC_q), .b({16{1'b0}}), .out(adder_2_out), .cin(1'b1));  // open: cout
  Multiplexer #(.enable("false"), .width(16)) multiplexer_1 (
    .in0(adder_2_out), .in1(bit_extender_1_out), .out(multiplexer_1_out), .sel(and_1_out));
  and and_1 (and_1_out, xor_1_out, decoder_jump);
  xor xor_1 (xor_1_out, decoder_loopback, and_3_out);
  Debouncer dbcr (.Pulse(dbcr_pulse), .Buttn(Input_valid), .Clk(Clk), .Rst(Rst));
  Decode decoder (
    .Opcode(program_data), .PtrOp(decoder_ptrop[15]), .MemOp(decoder_memop[7]), .LoopBack(decoder_loopback),
    .MemSrc(decoder_memsrc), .ModPtr(decoder_modptr), .Jump(decoder_jump), .Outp(out_enable),
    .ModMem(decoder_modmem), .Hold(decoder_hold));
  Register #(.width(16)) Pointer (.D(adder_1_out), .en(decoder_modptr), .clk(Clk), .Q(Pointer_q), .clr(Rst));
  or or_1 (or_1_out, dbcr_pulse, not_2_out);
  not not_2 (not_2_out, decoder_hold);
  Register #(.width(16)) PC (.D(multiplexer_1_out), .en(or_1_out), .clk(Clk), .Q(PC_q), .clr(Rst));
  not not_3 (not_3_out, decoder_modptr);
  Multiplexer #(.enable("false"), .width(16)) multiplexer_2 (
    .in0(adder_1_out), .in1(Pointer_q), .out(multiplexer_2_out), .sel(not_3_out));
  ROM #(.addrWidth(16), .dataWidth(16)) \program  (.addr(PC_q), .data({program_data_2, program_data}));
  Adder #(.width(16)) adder_3 (.a(next_ptr_q), .b({16{1'b0}}), .out(adder_3_out), .cin(1'b1));  // open: cout
  Comparator #(.width(16)) comparator_1 (.a(next_ptr_q), .b(multiplexer_2_out), .eq(comparator_1_eq));  // open: gt, lt
  Register #(.width(16)) next_ptr (.D(adder_3_out), .en(comparator_1_eq), .clk(Clk), .Q(next_ptr_q), .clr(Rst));
  or or_2 (or_2_out, decoder_modmem, comparator_1_eq);
  assign bit_extender_1_out = {{3{1'b0}}, program_data_2};  // Bit_Extender bit_extender_1
  RAM #(.addrWidth(16)) mem (
    .addr(multiplexer_2_out), .we(or_2_out), .oe(1'b1), .clk(Clk), .din(multiplexer_3_out),
    .dout({mem_dout[7], Char_out}));
  Multiplexer #(.enable("false"), .width(8)) multiplexer_3 (
    .in0(multiplexer_4_out), .in1({8{1'b0}}), .out(multiplexer_3_out), .sel(comparator_1_eq));
  not not_4 (not_4_out, decoder_memop[7]);
  nor nor_1 (nor_1_out, mem_dout[7], Char_out[6]);
  nor nor_2 (nor_2_out, Char_out[5], Char_out[4]);
  nor nor_3 (nor_3_out, Char_out[3], Char_out[2]);
  nor nor_4 (nor_4_out, Char_out[1], Char_out[0]);
  Adder adder_4 (
    .a({mem_dout[7], Char_out}), .b({8{decoder_memop[7]}}), .out(adder_4_out), .cin(not_4_out));  // open: cout
  Multiplexer #(.enable("false"), .width(8)) multiplexer_4 (
    .in0(adder_4_out), .in1(Key), .out(multiplexer_4_out), .sel(decoder_memsrc));
  and and_2 (and_2_out, nor_1_out, nor_2_out);
  and and_3 (and_3_out, and_2_out, and_4_out);
  and and_4 (and_4_out, nor_3_out, nor_4_out);

  // Notes on the sheet:
  //   contents of program (hex, n*v repeats v):
  //   0 1 8*2 19c 0 4*2 124 0 2 2 0 2 2 2 0 2 2 2 0 2 4*1 3 85 0 2 0 3 0 2 0 0 2 184 1 16d 1 3 55 0 0 6 0
  //   0 3 3 3 6 7*2 6 6 2 2 2 6 0 6 1 1 3 6 0 6 2 2 2 6 6*3 6 8*3 6 0 2 6 0 2 ffff
endmodule

module pipelined_demux (
  input  [7:0] data_in,
  input  [1:0] row,
  input  [1:0] col
);

  wire clock_1_out, demultiplexer_1_out0, demultiplexer_1_out1, demultiplexer_1_out2, demultiplexer_1_out3,
       demultiplexer_4_out0, demultiplexer_4_out1, demultiplexer_4_out2, demultiplexer_4_out3,
       demultiplexer_6_out0, demultiplexer_6_out1, demultiplexer_6_out2, demultiplexer_6_out3,
       demultiplexer_8_out0, demultiplexer_8_out1, demultiplexer_8_out2, demultiplexer_8_out3,
       demultiplexer_10_out0, demultiplexer_10_out1, demultiplexer_10_out2, demultiplexer_10_out3;
  wire [1:0] register_2_q, register_4_q, register_6_q, register_8_q;
  wire [7:0] demultiplexer_2_out0, demultiplexer_2_out1, demultiplexer_2_out2, demultiplexer_2_out3,
       demultiplexer_3_out0, demultiplexer_3_out1, demultiplexer_3_out2, demultiplexer_3_out3,
       demultiplexer_5_out0, demultiplexer_5_out1, demultiplexer_5_out2, demultiplexer_5_out3,
       demultiplexer_7_out0, demultiplexer_7_out1, demultiplexer_7_out2, demultiplexer_7_out3,
       demultiplexer_9_out0, demultiplexer_9_out1, demultiplexer_9_out2, demultiplexer_9_out3, register_1_q,
       register_3_q, register_5_q, register_7_q, register_9_q, register_10_q, register_11_q, register_12_q,
       register_13_q, register_14_q, register_15_q, register_16_q, register_17_q, register_18_q,
       register_19_q, register_20_q, register_21_q, register_22_q, register_23_q, register_24_q;

  Clock clock_1 (.out(clock_1_out));
  Demultiplexer #(.enable("false"), .select(2)) demultiplexer_1 (
    .out0(demultiplexer_1_out0), .out1(demultiplexer_1_out1), .out2(demultiplexer_1_out2),
    .out3(demultiplexer_1_out3), .in(1'b1));  // open: sel
  Demultiplexer #(.enable("false"), .select(2), .width(8)) demultiplexer_2 (
    .out0(demultiplexer_2_out0), .out1(demultiplexer_2_out1), .out2(demultiplexer_2_out2),
    .out3(demultiplexer_2_out3), .in(data_in), .sel(row));
  Register register_1 (
    .D(demultiplexer_2_out0), .en(demultiplexer_1_out0), .clk(clock_1_out), .Q(register_1_q));  // open: clr
  Register #(.width(2)) register_2 (
    .D(col), .en(demultiplexer_1_out0), .clk(clock_1_out), .Q(register_2_q));  // open: clr
  Register register_3 (
    .D(demultiplexer_2_out1), .en(demultiplexer_1_out1), .clk(clock_1_out), .Q(register_3_q));  // open: clr
  Register #(.width(2)) register_4 (
    .D(col), .en(demultiplexer_1_out1), .clk(clock_1_out), .Q(register_4_q));  // open: clr
  Register register_5 (
    .D(demultiplexer_2_out2), .en(demultiplexer_1_out2), .clk(clock_1_out), .Q(register_5_q));  // open: clr
  Register #(.width(2)) register_6 (
    .D(col), .en(demultiplexer_1_out2), .clk(clock_1_out), .Q(register_6_q));  // open: clr
  Register register_7 (
    .D(demultiplexer_2_out3), .en(demultiplexer_1_out3), .clk(clock_1_out), .Q(register_7_q));  // open: clr
  Register #(.width(2)) register_8 (
    .D(col), .en(demultiplexer_1_out3), .clk(clock_1_out), .Q(register_8_q));  // open: clr
  Demultiplexer #(.enable("false"), .select(2), .width(8)) demultiplexer_3 (
    .out0(demultiplexer_3_out0), .out1(demultiplexer_3_out1), .out2(demultiplexer_3_out2),
    .out3(demultiplexer_3_out3), .in(register_1_q), .sel(register_2_q));
  Demultiplexer #(.enable("false"), .select(2)) demultiplexer_4 (
    .out0(demultiplexer_4_out0), .out1(demultiplexer_4_out1), .out2(demultiplexer_4_out2),
    .out3(demultiplexer_4_out3), .in(1'b1), .sel(register_2_q));
  Demultiplexer #(.enable("false"), .select(2), .width(8)) demultiplexer_5 (
    .out0(demultiplexer_5_out0), .out1(demultiplexer_5_out1), .out2(demultiplexer_5_out2),
    .out3(demultiplexer_5_out3), .in(register_3_q), .sel(register_4_q));
  Demultiplexer #(.enable("false"), .select(2)) demultiplexer_6 (
    .out0(demultiplexer_6_out0), .out1(demultiplexer_6_out1), .out2(demultiplexer_6_out2),
    .out3(demultiplexer_6_out3), .in(1'b1), .sel(register_4_q));
  Demultiplexer #(.enable("false"), .select(2), .width(8)) demultiplexer_7 (
    .out0(demultiplexer_7_out0), .out1(demultiplexer_7_out1), .out2(demultiplexer_7_out2),
    .out3(demultiplexer_7_out3), .in(register_5_q), .sel(register_6_q));
  Demultiplexer #(.enable("false"), .select(2)) demultiplexer_8 (
    .out0(demultiplexer_8_out0), .out1(demultiplexer_8_out1), .out2(demultiplexer_8_out2),
    .out3(demultiplexer_8_out3), .in(1'b1), .sel(register_6_q));
  Demultiplexer #(.enable("false"), .select(2), .width(8)) demultiplexer_9 (
    .out0(demultiplexer_9_out0), .out1(demultiplexer_9_out1), .out2(demultiplexer_9_out2),
    .out3(demultiplexer_9_out3), .in(register_7_q), .sel(register_8_q));
  Demultiplexer #(.enable("false"), .select(2)) demultiplexer_10 (
    .out0(demultiplexer_10_out0), .out1(demultiplexer_10_out1), .out2(demultiplexer_10_out2),
    .out3(demultiplexer_10_out3), .in(1'b1), .sel(register_8_q));
  Register register_9 (
    .D(demultiplexer_3_out0), .en(demultiplexer_4_out0), .clk(clock_1_out), .Q(register_9_q));  // open: clr
  Register register_10 (
    .D(demultiplexer_3_out1), .en(demultiplexer_4_out1), .clk(clock_1_out), .Q(register_10_q));  // open: clr
  Register register_11 (
    .D(demultiplexer_3_out2), .en(demultiplexer_4_out2), .clk(clock_1_out), .Q(register_11_q));  // open: clr
  Register register_12 (
    .D(demultiplexer_3_out3), .en(demultiplexer_4_out3), .clk(clock_1_out), .Q(register_12_q));  // open: clr
  Register register_13 (
    .D(demultiplexer_5_out0), .en(demultiplexer_6_out0), .clk(clock_1_out), .Q(register_13_q));  // open: clr
  Register register_14 (
    .D(demultiplexer_5_out1), .en(demultiplexer_6_out1), .clk(clock_1_out), .Q(register_14_q));  // open: clr
  Register register_15 (
    .D(demultiplexer_5_out2), .en(demultiplexer_6_out2), .clk(clock_1_out), .Q(register_15_q));  // open: clr
  Register register_16 (
    .D(demultiplexer_5_out3), .en(demultiplexer_6_out3), .clk(clock_1_out), .Q(register_16_q));  // open: clr
  Register register_17 (
    .D(demultiplexer_7_out0), .en(demultiplexer_8_out0), .clk(clock_1_out), .Q(register_17_q));  // open: clr
  Register register_18 (
    .D(demultiplexer_7_out1), .en(demultiplexer_8_out1), .clk(clock_1_out), .Q(register_18_q));  // open: clr
  Register register_19 (
    .D(demultiplexer_7_out2), .en(demultiplexer_8_out2), .clk(clock_1_out), .Q(register_19_q));  // open: clr
  Register register_20 (
    .D(demultiplexer_7_out3), .en(demultiplexer_8_out3), .clk(clock_1_out), .Q(register_20_q));  // open: clr
  Register register_21 (
    .D(demultiplexer_9_out0), .en(demultiplexer_10_out0), .clk(clock_1_out), .Q(register_21_q));  // open: clr
  Register register_22 (
    .D(demultiplexer_9_out1), .en(demultiplexer_10_out1), .clk(clock_1_out), .Q(register_22_q));  // open: clr
  Register register_23 (
    .D(demultiplexer_9_out2), .en(demultiplexer_10_out2), .clk(clock_1_out), .Q(register_23_q));  // open: clr
  Register register_24 (
    .D(demultiplexer_9_out3), .en(demultiplexer_10_out3), .clk(clock_1_out), .Q(register_24_q));  // open: clr
  Hex_Digit_Display hex_digit_display_1 (.value(register_9_q[7:4]));  // open: dp
  Hex_Digit_Display hex_digit_display_2 (.value(register_9_q[3:0]));  // open: dp
  Hex_Digit_Display hex_digit_display_3 (.value(register_10_q[7:4]));  // open: dp
  Hex_Digit_Display hex_digit_display_4 (.value(register_10_q[3:0]));  // open: dp
  Hex_Digit_Display hex_digit_display_5 (.value(register_11_q[7:4]));  // open: dp
  Hex_Digit_Display hex_digit_display_6 (.value(register_11_q[3:0]));  // open: dp
  Hex_Digit_Display hex_digit_display_7 (.value(register_12_q[7:4]));  // open: dp
  Hex_Digit_Display hex_digit_display_8 (.value(register_12_q[3:0]));  // open: dp
  Hex_Digit_Display hex_digit_display_9 (.value(register_13_q[7:4]));  // open: dp
  Hex_Digit_Display hex_digit_display_10 (.value(register_13_q[3:0]));  // open: dp
  Hex_Digit_Display hex_digit_display_11 (.value(register_14_q[7:4]));  // open: dp
  Hex_Digit_Display hex_digit_display_12 (.value(register_14_q[3:0]));  // open: dp
  Hex_Digit_Display hex_digit_display_13 (.value(register_15_q[7:4]));  // open: dp
  Hex_Digit_Display hex_digit_display_14 (.value(register_15_q[3:0]));  // open: dp
  Hex_Digit_Display hex_digit_display_15 (.value(register_16_q[7:4]));  // open: dp
  Hex_Digit_Display hex_digit_display_16 (.value(register_16_q[3:0]));  // open: dp
  Hex_Digit_Display hex_digit_display_17 (.value(register_17_q[7:4]));  // open: dp
  Hex_Digit_Display hex_digit_display_18 (.value(register_17_q[3:0]));  // open: dp
  Hex_Digit_Display hex_digit_display_19 (.value(register_18_q[7:4]));  // open: dp
  Hex_Digit_Display hex_digit_display_20 (.value(register_18_q[3:0]));  // open: dp
  Hex_Digit_Display hex_digit_display_21 (.value(register_19_q[7:4]));  // open: dp
  Hex_Digit_Display hex_digit_display_22 (.value(register_19_q[3:0]));  // open: dp
  Hex_Digit_Display hex_digit_display_23 (.value(register_20_q[7:4]));  // open: dp
  Hex_Digit_Display hex_digit_display_24 (.value(register_20_q[3:0]));  // open: dp
  Hex_Digit_Display hex_digit_display_25 (.value(register_21_q[7:4]));  // open: dp
  Hex_Digit_Display hex_digit_display_26 (.value(register_21_q[3:0]));  // open: dp
  Hex_Digit_Display hex_digit_display_27 (.value(register_22_q[7:4]));  // open: dp
  Hex_Digit_Display hex_digit_display_28 (.value(register_22_q[3:0]));  // open: dp
  Hex_Digit_Display hex_digit_display_29 (.value(register_23_q[7:4]));  // open: dp
  Hex_Digit_Display hex_digit_display_30 (.value(register_23_q[3:0]));  // open: dp
  Hex_Digit_Display hex_digit_display_31 (.value(register_24_q[7:4]));  // open: dp
  Hex_Digit_Display hex_digit_display_32 (.value(register_24_q[3:0]));  // open: dp
endmodule

module pot_playground (
  input  H,
  input  V
);

  wire and_1_out, and_2_out, bitposition_q, bram_text_q, charcode_out, charcol_q, charpos_q, charrow_q,
       cibr_q, cprd1_q, cprd2_q, fontaddr_out, fontrom_addr_q, HR0_q, HR1_q, HR2_q, HR3_q, HR4_q, HR5_q,
       HR6_q, not_1_out, not_2_out, not_3_out, not_4_out, not_5_out, not_6_out, not_7_out, VR0_q, VR1_q,
       VR2_q, VR3_q, VR4_q, VR5_q, VR6_q, xrange_out, yrange_out;

  D_Flip_Flop HR6 (.D(H), .Q(HR6_q));  // open: clk, Qn, preset, reset
  D_Flip_Flop charrow (.D(not_1_out), .Q(charrow_q));  // open: clk, Qn, preset, reset
  not not_1 (not_1_out, V);
  D_Flip_Flop VR6 (.D(V), .Q(VR6_q));  // open: clk, Qn, preset, reset
  D_Flip_Flop HR5 (.D(HR6_q), .Q(HR5_q));  // open: clk, Qn, preset, reset
  D_Flip_Flop cprd1 (.D(not_2_out), .Q(cprd1_q));  // open: clk, Qn, preset, reset
  not not_2 (not_2_out, charrow_q);
  D_Flip_Flop VR5 (.D(VR6_q), .Q(VR5_q));  // open: clk, Qn, preset, reset
  not not_3 (not_3_out, HR5_q);
  not not_4 (not_4_out, cprd1_q);
  D_Flip_Flop charcol (.D(not_3_out), .Q(charcol_q));  // open: clk, Qn, preset, reset
  D_Flip_Flop HR4 (.D(HR5_q), .Q(HR4_q));  // open: clk, Qn, preset, reset
  D_Flip_Flop cprd2 (.D(not_4_out), .Q(cprd2_q));  // open: clk, Qn, preset, reset
  D_Flip_Flop VR4 (.D(VR5_q), .Q(VR4_q));  // open: clk, Qn, preset, reset
  D_Flip_Flop charpos (.D(and_1_out), .Q(charpos_q));  // open: clk, Qn, preset, reset
  and and_1 (and_1_out, charcol_q, cprd2_q);
  D_Flip_Flop HR3 (.D(HR4_q), .Q(HR3_q));  // open: clk, Qn, preset, reset
  D_Flip_Flop VR3 (.D(VR4_q), .Q(VR3_q));  // open: clk, Qn, preset, reset
  D_Flip_Flop bram_text (.D(not_5_out), .Q(bram_text_q));  // open: clk, Qn, preset, reset
  not not_5 (not_5_out, charpos_q);
  D_Flip_Flop HR2 (.D(HR3_q), .Q(HR2_q));  // open: clk, Qn, preset, reset
  D_Flip_Flop VR2 (.D(VR3_q), .Q(VR2_q));  // open: clk, Qn, preset, reset
  and fontaddr (fontaddr_out, VR2_q, charcode_out);
  not charcode (charcode_out, bram_text_q);
  D_Flip_Flop HR1 (.D(HR2_q), .Q(HR1_q));  // open: clk, Qn, preset, reset
  D_Flip_Flop VR1 (.D(VR2_q), .Q(VR1_q));  // open: clk, Qn, preset, reset
  D_Flip_Flop fontrom_addr (.D(fontaddr_out), .Q(fontrom_addr_q));  // open: clk, Qn, preset, reset
  D_Flip_Flop HR0 (.D(HR1_q), .Q(HR0_q));  // open: clk, Qn, preset, reset
  D_Flip_Flop bitposition (.D(not_6_out), .Q(bitposition_q));  // open: clk, Qn, preset, reset
  not not_6 (not_6_out, HR1_q);
  D_Flip_Flop VR0 (.D(VR1_q), .Q(VR0_q));  // open: clk, Qn, preset, reset
  D_Flip_Flop cibr (.D(not_7_out), .Q(cibr_q));  // open: clk, Qn, preset, reset
  not not_7 (not_7_out, fontrom_addr_q);
  not xrange (xrange_out, HR0_q);
  not yrange (yrange_out, VR0_q);
  D_Flip_Flop pixel (.D(and_2_out));  // open: clk, Q, Qn, preset, reset
  and and_2 (and_2_out, yrange_out, xrange_out, bitposition_q, cibr_q);
endmodule
