// Logisim project BF_Processor.circ as structural Verilog: 8 circuits, main circuit main
module main (
  input  [7:0] KeyIn
);

  wire and_1_out, and_2_out, and_3_out, and_4_out, and_5_out, Clk_out, Control_hold, Control_jump,
       Control_loopback, Control_memop, Control_memsrc, Control_modmem, Control_modptr, Control_output,
       Control_ptrop, d_ff_1_q, d_ff_2_q, Input_Valid_out, nor_1_out, nor_2_out, nor_3_out, nor_4_out,
       not_1_out, not_2_out, not_3_out, or_1_out, Reset_out, xor_1_out;
  wire [2:0] rom_1_data;
  wire [3:0] PC_q, pm1_8_1_out, pm1_8_1_out_2, Ptr_q, Ptr_q_2, Ptr_q_3, Ptr_q_4;
  wire [3:3] multiplexer_6_out_2;
  wire [6:0] multiplexer_6_out;
  wire [7:0] controlled_buffer_1_out, multiplexer_5_out, ram_1_data, register_1_q;
  wire [15:0] adder_1_out, bit_extender_1_out, multiplexer_1_out, multiplexer_2_out, multiplexer_3_out,
       multiplexer_4_out, pm1_16_1_out;
  wire [15:3] rom_1_data_2;
  wire [15:4] PC_q_2;

  D_Flip_Flop d_ff_1 (.D(Input_Valid_out), .clk(Clk_out), .Q(d_ff_1_q), .reset(Reset_out));  // open: Qn, preset
  D_Flip_Flop d_ff_2 (.D(d_ff_1_q), .clk(Clk_out), .Q(d_ff_2_q), .reset(Reset_out));  // open: Qn, preset
  Clock Clk (.out(Clk_out));
  Button Reset (.out(Reset_out));
  Button Input_Valid (.out(Input_Valid_out));
  Hex_Digit_Display hex_digit_display_1 (.value(Ptr_q_4));  // open: dp
  Control_v2 Control (
    .Opcode(rom_1_data), .PtrOp(Control_ptrop), .MemOp(Control_memop), .LoopBack(Control_loopback),
    .MemSrc(Control_memsrc), .ModPtr(Control_modptr), .Jump(Control_jump), .Output(Control_output),
    .ModMem(Control_modmem), .Hold(Control_hold));
  Hex_Digit_Display hex_digit_display_2 (.value(Ptr_q_2));  // open: dp
  Hex_Digit_Display hex_digit_display_3 (.value(Ptr_q_3));  // open: dp
  not not_1 (not_1_out, Clk_out);
  Multiplexer #(.width(16), .enable("false")) multiplexer_1 (
    .in0({Ptr_q_4, Ptr_q_3, Ptr_q_2, Ptr_q}), .in1(pm1_16_1_out), .out(multiplexer_1_out),
    .sel(Control_modptr));
  PM1_16 pm1_16_1 (.A({Ptr_q_4, Ptr_q_3, Ptr_q_2, Ptr_q}), .Op(Control_ptrop), .Out(pm1_16_1_out));
  Hex_Digit_Display hex_digit_display_4 (.value(Ptr_q));  // open: dp
  Adder #(.width(16)) adder_1 (.a({PC_q_2, PC_q}), .b({16{1'b0}}), .out(adder_1_out), .cin(1'b1));  // open: cout
  Multiplexer #(.width(16), .enable("false")) multiplexer_2 (
    .in0(adder_1_out), .in1(bit_extender_1_out), .out(multiplexer_2_out), .sel(and_1_out));
  xor xor_1 (xor_1_out, Control_loopback, and_5_out);
  and and_1 (and_1_out, xor_1_out, Control_jump);
  not not_2 (not_2_out, Control_hold);
  Register #(.width(16)) Ptr (
    .D(multiplexer_1_out), .en(1'b1), .clk(not_1_out), .Q({Ptr_q_4, Ptr_q_3, Ptr_q_2, Ptr_q}), .clr(Reset_out));
  Register #(.width(16)) PC (.D(multiplexer_3_out), .en(1'b1), .clk(Clk_out), .Q({PC_q_2, PC_q}), .clr(Reset_out));
  Multiplexer #(.width(16), .enable("false")) multiplexer_3 (
    .in0({PC_q_2, PC_q}), .in1(multiplexer_2_out), .out(multiplexer_3_out), .sel(or_1_out));
  or or_1 (or_1_out, not_2_out, d_ff_2_q);
  and and_2 (and_2_out, not_1_out, Control_modmem);
  RAM #(.addrWidth(13), .trigger("high")) ram_1 (
    .addr(multiplexer_4_out[12:0]), .we(and_2_out), .oe(not_3_out), .data(ram_1_data));
  Multiplexer #(.width(16), .enable("false")) multiplexer_4 (
    .in0(multiplexer_1_out), .in1({Ptr_q_4, Ptr_q_3, Ptr_q_2, Ptr_q}), .out(multiplexer_4_out),
    .sel(not_1_out));
  not not_3 (not_3_out, and_2_out);
  ROM #(.addrWidth(16), .dataWidth(16)) rom_1 (.addr({PC_q_2, PC_q}), .data({rom_1_data_2, rom_1_data}));
  assign bit_extender_1_out = {{3{1'b0}}, rom_1_data_2};  // Bit_Extender bit_extender_1
  TTY #(.rows(18), .cols(64)) tty_1 (.data(multiplexer_6_out), .clk(not_1_out), .we(Control_output), .clr(Reset_out));
  assign controlled_buffer_1_out = not_3_out ? ram_1_data : 8'bz;  // Controlled_Buffer controlled_buffer_1
  assign ram_1_data = and_2_out ? register_1_q : 8'bz;  // Controlled_Buffer controlled_buffer_2
  Hex_Digit_Display hex_digit_display_5 (.value(PC_q_2[11:8]));  // open: dp
  Hex_Digit_Display hex_digit_display_6 (.value(PC_q_2[15:12]));  // open: dp
  PM1_8 pm1_8_1 (.A(controlled_buffer_1_out), .Op(Control_memop), .Out({pm1_8_1_out_2, pm1_8_1_out}));
  Register register_1 (.D(multiplexer_5_out), .en(1'b1), .clk(and_2_out), .Q(register_1_q), .clr(Reset_out));
  Hex_Digit_Display hex_digit_display_7 (.value(PC_q_2[7:4]));  // open: dp
  Hex_Digit_Display hex_digit_display_8 (.value(PC_q));  // open: dp
  Hex_Digit_Display hex_digit_display_9 (.value(pm1_8_1_out_2));  // open: dp
  Multiplexer #(.width(8), .enable("false")) multiplexer_5 (
    .in0({pm1_8_1_out_2, pm1_8_1_out}), .in1(KeyIn), .out(multiplexer_5_out), .sel(Control_memsrc));
  Multiplexer #(.width(8), .enable("false")) multiplexer_6 (
    .in0(controlled_buffer_1_out), .in1(register_1_q), .out({multiplexer_6_out_2[3], multiplexer_6_out}),
    .sel(and_2_out));
  Hex_Digit_Display hex_digit_display_10 (.value(pm1_8_1_out));  // open: dp
  nor nor_1 (nor_1_out, multiplexer_6_out_2[3], multiplexer_6_out[6]);
  nor nor_2 (nor_2_out, multiplexer_6_out[5], multiplexer_6_out[4]);
  nor nor_3 (nor_3_out, multiplexer_6_out[3], multiplexer_6_out[2]);
  nor nor_4 (nor_4_out, multiplexer_6_out[1], multiplexer_6_out[0]);
  Hex_Digit_Display hex_digit_display_11 (.value(multiplexer_6_out[3:0]));  // open: dp
  Hex_Digit_Display hex_digit_display_12 (.value({multiplexer_6_out_2[3], multiplexer_6_out[6:4]}));  // open: dp
  and and_3 (and_3_out, nor_1_out, nor_2_out);
  and and_4 (and_4_out, nor_3_out, nor_4_out);
  and and_5 (and_5_out, and_3_out, and_4_out);

  // Notes on the sheet:
  //   Memory Pointer
  //   START CLK @ HIGH
  //   contents of rom_1 (hex, n*v repeats v):
  //   8*2 18c 0 4*2 114 0 2 2 0 2 2 2 0 2 2 2 0 2 4*1 3 75 0 2 0 3 0 2 0 0 2 174 1 15d 1 3 45 0 0 6 0 0 3
  //   3 3 6 7*2 6 6 2 2 2 6 0 6 1 1 3 6 0 6 2 2 2 6 6*3 6 8*3 6 0 2 6 0 2 2 6 ffff 1 1 2e5 6*0 27d 0 0 3ec
  //   4*0 3bd 4*1 44c 1 1 2 1 2 1 40d 1 1 a1c 6*0 524 4fc 4*1 2 4*0 3 49d 4*0 495 8*1 594 4*1 565 0 0 3
  //   5ec 1 1 2 0 0 3 5ad 2 1 1 7cc 3 4*0 774 3 684 2 4*0 3 645 3 1 1 3 6dc
  //   Program Counter
  //   ALU Result
  //   Memory I/O
endmodule

module PM_8 (
  input  [7:0] A,
  input  [7:0] B,
  input  C,
  output [7:0] Out
);

  wire [7:0] xor_1_out;

  assign xor_1_out = B ^ {8{C}};  // XOR_Gate xor_1, 8 bits wide
  Adder adder_1 (.a(A), .b(xor_1_out), .out(Out), .cin(C));  // open: cout
endmodule

module PM1_8 (
  input  [7:0] A,
  input  Op,
  output [7:0] Out
);

  PM_8 pm_8_1 (.A(A), .B(8'h1), .C(Op), .Out(Out));
endmodule

module PM_16 (
  input  [15:0] A,
  input  [15:0] B,
  input  C,
  output [15:0] Out
);

  wire [15:0] xor_1_out;

  assign xor_1_out = B ^ {16{C}};  // XOR_Gate xor_1, 16 bits wide
  Adder #(.width(16)) adder_1 (.a(A), .b(xor_1_out), .out(Out), .cin(C));  // open: cout
endmodule

module PM1_16 (
  input  [15:0] A,
  input  Op,
  output [15:0] Out
);

  PM_16 pm_16_1 (.A(A), .B(16'h1), .C(Op), .Out(Out));
endmodule

module Control (
  input  [2:0] Opcode,
  output PtrOp,
  output MemOp,
  output LoopBack,
  output MemSrc,
  output ModPtr,
  output Jump,
  output Output,
  output ModMem
);

  wire and_2_out, and_3_out, and_4_out, nor_2_out, not_1_out, not_2_out, not_3_out;

  not not_1 (not_1_out, Opcode[2]);
  not not_2 (not_2_out, Opcode[0]);
  not not_3 (not_3_out, Opcode[1]);
  nor nor_1 (ModPtr, Opcode[1], Opcode[2]);
  and and_1 (Jump, not_3_out, Opcode[2]);
  and and_2 (and_2_out, Opcode[1], Opcode[2]);
  and and_3 (and_3_out, Opcode[0], Opcode[1]);
  and and_4 (and_4_out, Opcode[1], not_1_out);
  and and_5 (Output, and_2_out, not_2_out);
  nor nor_2 (nor_2_out, and_3_out, and_4_out);
  not not_4 (ModMem, nor_2_out);

  assign LoopBack = Opcode[0];
  assign MemOp = Opcode[0];
  assign MemSrc = Opcode[2];
  assign PtrOp = Opcode[0];
endmodule

module Control_v2 (
  input  [2:0] Opcode,
  output PtrOp,
  output MemOp,
  output LoopBack,
  output MemSrc,
  output ModPtr,
  output Jump,
  output Output,
  output ModMem,
  output Hold
);

  wire and_1_out, and_2_out, nor_3_out, nor_4_out, not_1_out;

  not not_1 (not_1_out, Opcode[2]);
  nor nor_1 (ModPtr, Opcode[1], Opcode[2]);
  nor nor_2 (Jump, Opcode[1], not_1_out);
  nor nor_3 (nor_3_out, Opcode[0], not_1_out);
  and and_1 (and_1_out, Opcode[1], not_1_out);
  and and_2 (and_2_out, Opcode[0], Opcode[1]);
  and and_3 (Output, nor_3_out, Opcode[1]);
  nor nor_4 (nor_4_out, and_1_out, and_2_out);
  not not_2 (ModMem, nor_4_out);
  and and_4 (Hold, and_2_out, Opcode[2]);

  assign LoopBack = Opcode[0];
  assign MemOp = Opcode[0];
  assign MemSrc = Opcode[2];
  assign PtrOp = Opcode[0];
endmodule

module Test (
  input  in_1,
  input  in_2,
  input  in_3,
  input  [7:0] in_4
);

  wire and_1_out, button_1_out, button_2_out, button_3_out, button_4_out, clock_1_out, d_ff_1_q, d_ff_2_q,
       multiplexer_1_out, multiplexer_2_out, not_1_out, not_2_out, rgbled_1_p1;
  wire [7:0] control_1_ptrop, control_v2_1_ptrop, pm1_8_1_p1, pm1_8_1_p3, xnor_1_out;

  Clock clock_1 (.out(clock_1_out));
  // PM1_8 pm1_8_1: pin names not known; wires that end beside it: pm1_8_1_p1, 1'b0, pm1_8_1_p3
  Button button_1 (.out(button_1_out));
  Button button_2 (.out(button_2_out));
  not not_1 (not_1_out, d_ff_1_q);
  Multiplexer #(.enable("false")) multiplexer_1 (.in0(in_2), .in1(in_3), .out(multiplexer_1_out), .sel(d_ff_1_q));
  Register register_1 (.D(pm1_8_1_p3), .en(1'b1), .clk(button_1_out), .Q(pm1_8_1_p1), .clr(button_2_out));
  D_Flip_Flop d_ff_1 (.D(not_1_out), .clk(multiplexer_1_out), .Q(d_ff_1_q));  // open: Qn, preset, reset
  Control control_1 (
    .Opcode(pm1_8_1_p1[2:0]), .PtrOp(control_1_ptrop[0]), .MemOp(control_1_ptrop[1]),
    .LoopBack(control_1_ptrop[2]), .MemSrc(control_1_ptrop[3]), .ModPtr(control_1_ptrop[4]),
    .Jump(control_1_ptrop[5]), .Output(control_1_ptrop[6]), .ModMem(control_1_ptrop[7]));
  Control_v2 control_v2_1 (
    .Opcode(pm1_8_1_p1[2:0]), .PtrOp(control_v2_1_ptrop[0]), .MemOp(control_v2_1_ptrop[1]),
    .LoopBack(control_v2_1_ptrop[2]), .MemSrc(control_v2_1_ptrop[3]), .ModPtr(control_v2_1_ptrop[4]),
    .Jump(control_v2_1_ptrop[5]), .Output(control_v2_1_ptrop[6]), .ModMem(control_v2_1_ptrop[7]));  // open: Hold
  D_Flip_Flop d_ff_2 (.D(not_2_out), .clk(multiplexer_2_out), .Q(d_ff_2_q));  // open: Qn, preset, reset
  not not_2 (not_2_out, d_ff_2_q);
  Multiplexer #(.enable("false")) multiplexer_2 (
    .in0(in_3), .in1(clock_1_out), .out(multiplexer_2_out), .sel(d_ff_2_q));
  assign xnor_1_out = ~(control_1_ptrop ^ control_v2_1_ptrop);  // XNOR_Gate xnor_1, 8 bits wide
  or or_1 (in_1, clock_1_out, d_ff_1_q, d_ff_2_q);
  and and_1 (and_1_out, xnor_1_out[0], xnor_1_out[0], xnor_1_out[1], xnor_1_out[2], xnor_1_out[3], xnor_1_out[4], xnor_1_out[5], xnor_1_out[6], xnor_1_out[7]);
  Hex_Digit_Display hex_digit_display_1 (.value(in_4[7:4]));  // open: dp
  Hex_Digit_Display hex_digit_display_2 (.value(in_4[3:0]));  // open: dp
  Button button_3 (.out(button_3_out));
  Button button_4 (.out(button_4_out));
  // RGBLED rgbled_1: pin names not known; wires that end beside it: rgbled_1_p1, and_1_out
  not not_3 (rgbled_1_p1, and_1_out);
  TTY tty_1 (.data(in_4[6:0]), .clk(button_3_out), .clr(button_4_out));  // open: we
endmodule
