// Logisim project BF_Processor_BOM.circ as structural Verilog: 5 circuits, main circuit BFProcessor_BOM
module ROM (
  input  [16:0] A,
  input  CEn,
  input  OEn,
  input  PGMn,
  output [7:0] D
);

  wire and_1_out;
  wire [7:0] rom_1_data;

  ROM_part #(.addrWidth(17)) rom_1 (.addr(A), .data(rom_1_data));
  and and_1 (and_1_out, ~CEn, ~OEn);  // AND_Gate
  assign D = and_1_out ? rom_1_data : 8'bz;  // Controlled_Buffer controlled_buffer_1
endmodule

module BFProcessor_BOM (
  input  Input_Valid
);

  wire adder_1_cout, adder_2_cout, adder_3_cout, CLK_out, undriven, undriven_2, undriven_3, undriven_4,
       undriven_5, undriven_6, undriven_7;
  wire [2:0] ROM_LSBs_d_2;
  wire [3:0] adder_1_out, adder_2_out, adder_3_out, adder_4_out, mux4_1_y, mux4_2_y, mux4_3_y, mux4_4_y;
  wire [12:0] ROM_LSBs_d;
  wire [15:0] PC_LSBs_q;

  Clock CLK (.out(CLK_out));
  Adder #(.width(4)) adder_1 (.a(PC_LSBs_q[3:0]), .b(4'b0000), .out(adder_1_out), .cin(1'b1), .cout(adder_1_cout));
  Adder #(.width(4)) adder_2 (
    .a(PC_LSBs_q[7:4]), .b(4'b0000), .out(adder_2_out), .cin(adder_1_cout), .cout(adder_2_cout));
  Adder #(.width(4)) adder_3 (
    .a(PC_LSBs_q[11:8]), .b(4'b0000), .out(adder_3_out), .cin(adder_2_cout), .cout(adder_3_cout));
  Adder #(.width(4)) adder_4 (.a(PC_LSBs_q[15:12]), .b(4'b0000), .out(adder_4_out), .cin(adder_3_cout));  // open: cout
  Mux4 mux4_1 (.I0(adder_1_out), .I1(ROM_LSBs_d[3:0]), .Sel(undriven), .E_n(1'b0), .Y(mux4_1_y));
  Mux4 mux4_2 (.I0(adder_2_out), .I1(ROM_LSBs_d[7:4]), .Sel(undriven), .E_n(1'b0), .Y(mux4_2_y));
  Mux4 mux4_3 (.I0(adder_3_out), .I1(ROM_LSBs_d[11:8]), .Sel(undriven), .E_n(1'b0), .Y(mux4_3_y));
  Mux4 mux4_4 (.I0(adder_4_out), .I1({3'b000, ROM_LSBs_d[12]}), .Sel(undriven), .E_n(1'b0), .Y(mux4_4_y));
  Reg8 PC_LSBs (.D({mux4_2_y, mux4_1_y}), .Clk(undriven_4), .OEn(undriven_3), .clr(undriven_2), .Q(PC_LSBs_q[7:0]));
  Reg8 PC_MSBs (.D({mux4_4_y, mux4_3_y}), .Clk(undriven_4), .OEn(undriven_3), .clr(undriven_2), .Q(PC_LSBs_q[15:8]));
  ROM ROM_LSBs (
    .A({1'b0, PC_LSBs_q}), .CEn(undriven_7), .OEn(undriven_6), .PGMn(undriven_5),
    .D({ROM_LSBs_d[4:0], ROM_LSBs_d_2}));
  ROM ROM_MSBs (.A({1'b0, PC_LSBs_q}), .CEn(undriven_7), .OEn(undriven_6), .PGMn(undriven_5), .D(ROM_LSBs_d[12:5]));

  // Notes on the sheet:
  //   CLK
  //   !CLK
  //   PtrOp
  //   MemOp
  //   Loopback
  //   ModMem
  //   Jump
  //   Modptr
  //   MemSrc
  //   Hold
  //   Output
endmodule

module Reg8 (
  input  [7:0] D,
  input  Clk,
  input  OEn,
  input  clr,
  output [7:0] Q
);

  wire not_1_out;
  wire [7:0] register_1_q;

  Register register_1 (.D(D), .en(1'b1), .clk(Clk), .Q(register_1_q), .clr(clr));
  not not_1 (not_1_out, OEn);
  assign Q = not_1_out ? register_1_q : 8'bz;  // Controlled_Buffer controlled_buffer_1
endmodule

module Tri_St8 (
  input  OE1n,
  input  OE2n,
  input  [7:0] A,
  output [7:0] Y
);

  wire and_1_out;

  and and_1 (and_1_out, ~OE1n, ~OE2n);  // AND_Gate
  assign Y = and_1_out ? A : 8'bz;  // Controlled_Buffer controlled_buffer_1
endmodule

module Mux4 (
  input  [3:0] I0,
  input  [3:0] I1,
  input  Sel,
  input  E_n,
  output [3:0] Y
);

  wire not_1_out;

  Multiplexer #(.width(4)) multiplexer_1 (.in0(I0), .in1(I1), .out(Y), .sel(Sel), .en(not_1_out));
  not not_1 (not_1_out, E_n);
endmodule
