// Logisim project BF_Processor_BOM_v2.circ as structural Verilog: 13 circuits, main circuit main
module main (
  input  [7:0] Char_In,
  input  In_G,
  input  [2:0] in_3
);

  wire adder_1_cout, adder_2_cout, adder_3_cout, adder_5_cout, adder_6_cout, adder_7_cout, adder_9_cout,
       and4_1_y1, and4_1_y2, and4_1_y3, and4_1_y4, and4_2_y1, and4_2_y2, and4_2_y3, and4_2_y4, and4_3_y1,
       and4_4_y1, and4_4_y2, and4_4_y3, and4_4_y4, Clk_out, inv6_1_o1, inv6_1_o3, inv6_1_o6, inv6_2_o2,
       inv6_2_o4, inv6_2_o5, inv6_3_o1, inv6_3_o2, nor4_1_y1, nor4_1_y2, nor4_1_y3, nor4_1_y4, nor4_2_y1,
       nor4_2_y2, nor4_2_y3, nor4_2_y4, Reset_out, xor4_1_y1;
  wire [2:1] rom_1_data;
  wire [3:0] adder_1_out, adder_2_out, adder_3_out, adder_4_out, adder_5_out, adder_6_out, adder_7_out,
       adder_8_out, adder_9_out, adder_10_out, ALU_Leg_q, ALU_Leg_q_2, mux4_1_o, mux4_2_o, mux4_3_o,
       mux4_4_o, mux4_5_o, mux4_6_o, mux4_7_o, mux4_8_o, mux4_9_o, mux4_10_o, mux4_11_o, mux4_12_o,
       mux4_13_o, mux4_14_o, Ptr_LSBs_q, Ptr_LSBs_q_2, Ptr_MSBs_q, Ptr_MSBs_q_2, tri_st8_1_o, tri_st8_1_o_2;
  wire [3:3] mux4_16_o, rom_1_data_3;
  wire [6:0] mux4_15_o;
  wire [7:0] tri_st8_2_o;
  wire [12:0] rom_1_data_2;
  wire [15:0] PC_LSBs_q;

  Button Reset (.out(Reset_out));
  Clock Clk (.out(Clk_out));
  INV6 inv6_1 (
    .I1(rom_1_data[2]), .O1(inv6_1_o1), .I3(rom_1_data_3[3]), .O3(inv6_1_o3), .GND(1'b0), .VCC(1'b1),
    .I6(nor4_1_y4), .O6(inv6_1_o6));  // open: I2, O2, I4, O4, I5, O5
  NOR4 nor4_1 (
    .Y1(nor4_1_y1), .B1(inv6_1_o1), .A1(rom_1_data[1]), .Y2(nor4_1_y2), .B2(inv6_1_o1), .A2(rom_1_data_3[3]),
    .GND(1'b0), .VCC(1'b1), .Y3(nor4_1_y3), .B3(rom_1_data[1]), .A3(rom_1_data[2]), .Y4(nor4_1_y4),
    .B4(and4_1_y3), .A4(and4_1_y1));
  AND4 and4_1 (
    .A1(inv6_1_o1), .B1(rom_1_data[1]), .Y1(and4_1_y1), .A2(nor4_1_y2), .B2(rom_1_data[1]), .Y2(and4_1_y2),
    .GND(1'b0), .VCC(1'b1), .A3(rom_1_data[1]), .B3(rom_1_data_3[3]), .Y3(and4_1_y3), .A4(and4_1_y3),
    .B4(rom_1_data[2]), .Y4(and4_1_y4));
  Adder #(.width(4)) adder_1 (.a(PC_LSBs_q[3:0]), .b(4'b0000), .out(adder_1_out), .cin(1'b1), .cout(adder_1_cout));
  Adder #(.width(4)) adder_2 (
    .a(PC_LSBs_q[7:4]), .b(4'b0000), .out(adder_2_out), .cin(adder_1_cout), .cout(adder_2_cout));
  Adder #(.width(4)) adder_3 (
    .a(PC_LSBs_q[11:8]), .b(4'b0000), .out(adder_3_out), .cin(adder_2_cout), .cout(adder_3_cout));
  Adder #(.width(4)) adder_4 (.a(PC_LSBs_q[15:12]), .b(4'b0000), .out(adder_4_out), .cin(adder_3_cout));  // open: cout
  XOR4 xor4_1 (
    .A1(and4_4_y1), .B1(rom_1_data_3[3]), .Y1(xor4_1_y1), .GND(1'b0), .VCC(1'b1));  // open: A2, B2, Y2, A3, B3, Y3, A4, B4, Y4
  AND4 and4_2 (
    .A1(xor4_1_y1), .B1(nor4_1_y1), .Y1(and4_2_y1), .A2(inv6_2_o2), .B2(and4_1_y4), .Y2(and4_2_y2),
    .GND(1'b0), .VCC(1'b1), .A3(inv6_2_o5), .B3(Clk_out), .Y3(and4_2_y3), .A4(inv6_2_o4), .B4(and4_2_y2),
    .Y4(and4_2_y4));
  INV6 inv6_2 (
    .I2(In_G), .O2(inv6_2_o2), .GND(1'b0), .VCC(1'b1), .I4(and4_2_y3), .O4(inv6_2_o4), .I5(and4_2_y4),
    .O5(inv6_2_o5));  // open: I1, O1, I3, O3, I6, O6
  Mux4 mux4_1 (.I0(adder_1_out), .I1(rom_1_data_2[3:0]), .Sel(and4_2_y1), .E_n(1'b0), .O(mux4_1_o));
  Mux4 mux4_2 (.I0(adder_2_out), .I1(rom_1_data_2[7:4]), .Sel(and4_2_y1), .E_n(1'b0), .O(mux4_2_o));
  Mux4 mux4_3 (.I0(adder_3_out), .I1(rom_1_data_2[11:8]), .Sel(and4_2_y1), .E_n(1'b0), .O(mux4_3_o));
  Mux4 mux4_4 (.I0(adder_4_out), .I1({3'b000, rom_1_data_2[12]}), .Sel(and4_2_y1), .E_n(1'b0), .O(mux4_4_o));
  Hex_Digit_Display hex_digit_display_1 (.value(PC_LSBs_q[15:12]));  // open: dp
  Reg8 PC_LSBs (.D({mux4_2_o, mux4_1_o}), .Clk(and4_2_y3), .OEn(1'b0), .clr(Reset_out), .Q(PC_LSBs_q[7:0]));
  Reg8 PC_MSBs (.D({mux4_4_o, mux4_3_o}), .Clk(and4_2_y3), .OEn(1'b0), .clr(Reset_out), .Q(PC_LSBs_q[15:8]));
  Hex_Digit_Display hex_digit_display_2 (.value(PC_LSBs_q[11:8]));  // open: dp
  Hex_Digit_Display hex_digit_display_3 (.value(PC_LSBs_q[7:4]));  // open: dp
  Adder #(.width(4)) adder_5 (
    .a(Ptr_LSBs_q), .b({4{rom_1_data_3[3]}}), .out(adder_5_out), .cin(inv6_1_o3), .cout(adder_5_cout));
  Adder #(.width(4)) adder_6 (
    .a(Ptr_LSBs_q_2), .b({4{rom_1_data_3[3]}}), .out(adder_6_out), .cin(adder_5_cout), .cout(adder_6_cout));
  Adder #(.width(4)) adder_7 (
    .a(Ptr_MSBs_q), .b({4{rom_1_data_3[3]}}), .out(adder_7_out), .cin(adder_6_cout), .cout(adder_7_cout));
  Adder #(.width(4)) adder_8 (
    .a(Ptr_MSBs_q_2), .b({4{rom_1_data_3[3]}}), .out(adder_8_out), .cin(adder_7_cout));  // open: cout
  ROM #(.addrWidth(17), .dataWidth(16)) rom_1 (
    .addr({1'b0, PC_LSBs_q}), .data({rom_1_data_2, rom_1_data, rom_1_data_3[3]}));
  Hex_Digit_Display hex_digit_display_4 (.value(PC_LSBs_q[3:0]));  // open: dp
  Mux4 mux4_5 (.I0(Ptr_LSBs_q), .I1(adder_5_out), .Sel(nor4_1_y3), .E_n(1'b0), .O(mux4_5_o));
  Mux4 mux4_6 (.I0(Ptr_LSBs_q_2), .I1(adder_6_out), .Sel(nor4_1_y3), .E_n(1'b0), .O(mux4_6_o));
  Mux4 mux4_7 (.I0(Ptr_MSBs_q), .I1(adder_7_out), .Sel(nor4_1_y3), .E_n(1'b0), .O(mux4_7_o));
  Mux4 mux4_8 (.I0(Ptr_MSBs_q_2), .I1(adder_8_out), .Sel(nor4_1_y3), .E_n(1'b0), .O(mux4_8_o));
  Reg8 Ptr_LSBs (
    .D({mux4_6_o, mux4_5_o}), .Clk(inv6_2_o4), .OEn(1'b0), .clr(Reset_out), .Q({Ptr_LSBs_q_2, Ptr_LSBs_q}));
  Reg8 Ptr_MSBs (
    .D({mux4_8_o, mux4_7_o}), .Clk(inv6_2_o4), .OEn(1'b0), .clr(Reset_out), .Q({Ptr_MSBs_q_2, Ptr_MSBs_q}));
  Mux4 mux4_9 (.I0(mux4_5_o), .I1(Ptr_LSBs_q), .Sel(inv6_2_o4), .E_n(1'b0), .O(mux4_9_o));
  Mux4 mux4_10 (.I0(mux4_6_o), .I1(Ptr_LSBs_q_2), .Sel(inv6_2_o4), .E_n(1'b0), .O(mux4_10_o));
  Mux4 mux4_11 (.I0(mux4_7_o), .I1(Ptr_MSBs_q), .Sel(inv6_2_o4), .E_n(1'b0), .O(mux4_11_o));
  Mux4 mux4_12 (.I0(mux4_8_o), .I1(Ptr_MSBs_q_2), .Sel(inv6_2_o4), .E_n(1'b0), .O(mux4_12_o));
  Adder #(.width(4)) adder_9 (
    .a(tri_st8_1_o), .b({4{rom_1_data_3[3]}}), .out(adder_9_out), .cin(inv6_3_o2), .cout(adder_9_cout));
  Adder #(.width(4)) adder_10 (
    .a(tri_st8_1_o_2), .b({4{rom_1_data_3[3]}}), .out(adder_10_out), .cin(adder_9_cout));  // open: cout
  Tri_St8 tri_st8_1 (.OE1n(and4_3_y1), .OE2n(and4_3_y1), .I(tri_st8_2_o), .O({tri_st8_1_o_2, tri_st8_1_o}));
  Tri_St8 tri_st8_2 (.OE1n(inv6_3_o1), .OE2n(inv6_3_o1), .I({ALU_Leg_q_2, ALU_Leg_q}), .O(tri_st8_2_o));
  RAM #(.addrWidth(13), .trigger("low")) ram_1 (
    .addr({mux4_12_o[0], mux4_11_o, mux4_10_o, mux4_9_o}), .we(inv6_3_o1), .oe(and4_3_y1), .data(tri_st8_2_o));
  Hex_Digit_Display hex_digit_display_5 (.value(Ptr_MSBs_q_2));  // open: dp
  Mux4 mux4_13 (.I0(adder_9_out), .I1(Char_In[3:0]), .Sel(rom_1_data[2]), .E_n(1'b0), .O(mux4_13_o));
  Mux4 mux4_14 (.I0(adder_10_out), .I1(Char_In[7:4]), .Sel(rom_1_data[2]), .E_n(1'b0), .O(mux4_14_o));
  Hex_Digit_Display hex_digit_display_6 (.value(Ptr_LSBs_q_2));  // open: dp
  Hex_Digit_Display hex_digit_display_7 (.value(Ptr_MSBs_q));  // open: dp
  Reg8 ALU_Leg (.D({mux4_14_o, mux4_13_o}), .Clk(and4_3_y1), .OEn(1'b0), .clr(Reset_out), .Q({ALU_Leg_q_2, ALU_Leg_q}));
  Mux4 mux4_15 (.I0(tri_st8_1_o), .I1(ALU_Leg_q), .Sel(and4_3_y1), .E_n(1'b0), .O(mux4_15_o[3:0]));
  Mux4 mux4_16 (.I0(tri_st8_1_o_2), .I1(ALU_Leg_q_2), .Sel(and4_3_y1), .E_n(1'b0), .O({mux4_16_o[3], mux4_15_o[6:4]}));
  TTY #(.rows(2)) tty_1 (.data(mux4_15_o), .clk(and4_4_y3), .clr(Reset_out));  // open: we
  Hex_Digit_Display hex_digit_display_8 (.value(Ptr_LSBs_q));  // open: dp
  INV6 inv6_3 (
    .I1(and4_3_y1), .O1(inv6_3_o1), .I2(rom_1_data_3[3]), .O2(inv6_3_o2), .GND(1'b0), .VCC(1'b1));  // open: I3, O3, I4, O4, I5, O5, I6, O6
  AND4 and4_3 (
    .A1(inv6_2_o4), .B1(inv6_1_o6), .Y1(and4_3_y1), .GND(1'b0), .VCC(1'b1));  // open: A2, B2, Y2, A3, B3, Y3, A4, B4, Y4
  Hex_Digit_Display hex_digit_display_9 (.value(mux4_14_o));  // open: dp
  Hex_Digit_Display hex_digit_display_10 (.value({mux4_16_o[3], mux4_15_o[6:4]}));  // open: dp
  AND4 and4_4 (
    .A1(and4_4_y4), .B1(and4_4_y2), .Y1(and4_4_y1), .A2(nor4_2_y2), .B2(nor4_2_y1), .Y2(and4_4_y2),
    .GND(1'b0), .VCC(1'b1), .A3(inv6_2_o4), .B3(and4_1_y2), .Y3(and4_4_y3), .A4(nor4_2_y4), .B4(nor4_2_y3),
    .Y4(and4_4_y4));
  NOR4 nor4_2 (
    .Y1(nor4_2_y1), .B1(mux4_15_o[0]), .A1(mux4_15_o[1]), .Y2(nor4_2_y2), .B2(mux4_15_o[2]),
    .A2(mux4_15_o[3]), .GND(1'b0), .VCC(1'b1), .Y3(nor4_2_y3), .B3(mux4_16_o[3]), .A3(mux4_15_o[6]),
    .Y4(nor4_2_y4), .B4(mux4_15_o[5]), .A4(mux4_15_o[4]));
  Hex_Digit_Display hex_digit_display_11 (.value(mux4_13_o));  // open: dp
  Hex_Digit_Display hex_digit_display_12 (.value(mux4_15_o[3:0]));  // open: dp

  // Notes on the sheet:
  //   Output
  //   START CLK @ HIGH
  //   !CLK
  //   PtrOp
  //   MemOp
  //   Loopback
  //   ModMem
  //   Jump
  //   ModPtr
  //   MemSrc
  //   Hold
  //   CLK
  //   !PtrOp
  //   Actually going to be 2x8-bit ROMs
  //   contents of rom_1 (hex, n*v repeats v):
  //   8*2 18c 0 4*2 114 0 2 2 0 2 2 2 0 2 2 2 0 2 4*1 3 75 0 2 0 3 0 2 0 0 2 174 1 15d 1 3 45 0 0 6 0 0 3
  //   3 3 6 7*2 6 6 2 2 2 6 0 6 1 1 3 6 0 6 2 2 2 6 6*3 6 8*3 6 0 2 6 0 2 2 6 ffff 1 1 2e5 6*0 27d 0 0 3ec
  //   4*0 3bd 4*1 44c 1 1 2 1 2 1 40d 1 1 a1c 6*0 524 4fc 4*1 2 4*0 3 49d 4*0 495 8*1 594 4*1 565 0 0 3
  //   5ec 1 1 2 0 0 3 5ad 2 1 1 7cc 3 4*0 774 3 684 2 4*0 3 645 3 1 1 3 6dc
  //   MSBs
  //   LSBs
  //   Could also use 2x4-pin NOR?
endmodule

module Reg8 (
  input  [7:0] D,
  input  Clk,
  input  OEn,
  input  clr,
  output [7:0] Q
);

  wire not_1_out;
  wire [7:0] register_1_q;

  Register register_1 (.D(D), .en(1'b1), .clk(Clk), .Q(register_1_q), .clr(clr));
  not not_1 (not_1_out, OEn);
  assign Q = not_1_out ? register_1_q : 8'bz;  // Controlled_Buffer controlled_buffer_1
endmodule

module Tri_St8 (
  input  OE1n,
  input  OE2n,
  input  [7:0] I,
  output [7:0] O
);

  wire and_1_out;

  and and_1 (and_1_out, ~OE1n, ~OE2n);  // AND_Gate
  assign O = and_1_out ? I : 8'bz;  // Controlled_Buffer controlled_buffer_1
endmodule

module Mux4 (
  input  [3:0] I0,
  input  [3:0] I1,
  input  Sel,
  input  E_n,
  output [3:0] O
);

  wire not_1_out;

  Multiplexer #(.width(4)) multiplexer_1 (.in0(I0), .in1(I1), .out(O), .sel(Sel), .en(not_1_out));
  not not_1 (not_1_out, E_n);
endmodule

module NAND4 (
  input  A1,
  input  VCC,
  input  B1,
  input  A3,
  input  B3,
  input  A2,
  input  B2,
  input  A4,
  input  B4,
  input  GND,
  output Y1,
  output Y3,
  output Y2,
  output Y4
);

  nand nand_1 (Y1, B1, A1);
  nand nand_2 (Y2, B2, A2);
  nand nand_3 (Y3, A3, B3);
  nand nand_4 (Y4, A4, B4);

  // Notes on the sheet:
  //   7400: quad NAND
endmodule

// NORs
module NOR4 (
  input  VCC,
  input  B1,
  input  A1,
  input  B3,
  input  A3,
  input  B2,
  input  A2,
  input  B4,
  input  GND,
  input  A4,
  output Y1,
  output Y3,
  output Y2,
  output Y4
);

  nor nor_1 (Y1, B1, A1);
  nor nor_2 (Y2, B2, A2);
  nor nor_3 (Y3, A3, B3);
  nor nor_4 (Y4, A4, B4);

  // Notes on the sheet:
  //   7402: quad NOR
endmodule

// NOTs
module INV6 (
  input  I1,
  input  VCC,
  input  I4,
  input  I2,
  input  I5,
  input  I3,
  input  I6,
  input  GND,
  output O1,
  output O4,
  output O2,
  output O5,
  output O3,
  output O6
);

  not not_1 (O1, I1);
  not not_2 (O2, I2);
  not not_3 (O3, I3);
  not not_4 (O4, I4);
  not not_5 (O5, I5);
  not not_6 (O6, I6);

  // Notes on the sheet:
  //   7407: hex inverter
endmodule

// ANDs
module AND4 (
  input  A1,
  input  VCC,
  input  B1,
  input  A3,
  input  B3,
  input  A2,
  input  B2,
  input  A4,
  input  B4,
  input  GND,
  output Y1,
  output Y3,
  output Y2,
  output Y4
);

  and and_1 (Y1, B1, A1);
  and and_2 (Y2, B2, A2);
  and and_3 (Y3, A3, B3);
  and and_4 (Y4, A4, B4);

  // Notes on the sheet:
  //   7408: quad AND
endmodule

// XORs
module XOR4 (
  input  A1,
  input  VCC,
  input  B1,
  input  A3,
  input  B3,
  input  A2,
  input  B2,
  input  A4,
  input  B4,
  input  GND,
  output Y1,
  output Y3,
  output Y2,
  output Y4
);

  xor xor_1 (Y1, B1, A1);
  xor xor_2 (Y2, B2, A2);
  xor xor_3 (Y3, A3, B3);
  xor xor_4 (Y4, A4, B4);

  // Notes on the sheet:
  //   7486: quad XOR
endmodule

module AND2 (
  input  A1,
  input  VCC,
  input  B1,
  input  A2,
  input  NC1,
  input  B2,
  input  C1,
  input  NC2,
  input  D1,
  input  C2,
  input  D2,
  input  GND,
  output Y1,
  output Y2
);

  and and_1 (Y1, D1, C1, B1, A1);
  and and_2 (Y2, A2, B2, C2, D2);

  // Notes on the sheet:
  //   7421: dual 4-input AND
endmodule

module NOR2 (
  input  A1,
  input  VCC,
  input  B1,
  input  A2,
  input  NC1,
  input  B2,
  input  C1,
  input  NC2,
  input  D1,
  input  C2,
  input  D2,
  input  GND,
  output Y1,
  output Y2
);

  nor nor_1 (Y1, D1, C1, B1, A1);
  nor nor_2 (Y2, A2, B2, C2, D2);

  // Notes on the sheet:
  //   7425: dual 4-input NOR
endmodule

module OR4 (
  input  A1,
  input  YCC,
  input  B1,
  input  A3,
  input  B3,
  input  A2,
  input  B2,
  input  A4,
  input  B4,
  input  GND,
  output Y1,
  output Y3,
  output Y2,
  output Y4
);

  or or_1 (Y1, B1, A1);
  or or_2 (Y2, B2, A2);
  or or_3 (Y3, A3, B3);
  or or_4 (Y4, A4, B4);

  // Notes on the sheet:
  //   7432: quad OR
endmodule

module Test (
  input  [2:0] in_1,
  output PtrOp,
  output MemOp,
  output Loopback,
  output Memsrc,
  output Modptr,
  output Jump,
  output WriteOut,
  output ModMem,
  output Hold
);

  wire and4_1_y1, and4_1_y3, and_1_out, and_2_out, and_5_out, inv6_1_o1, nor4_1_y2, nor4_1_y4, nor_3_out,
       nor_4_out, not_1_out, rgbled_1_p1;
  wire [8:0] xnor_1_out;
  wire [8:4] nor4_1_y3;

  not not_1 (not_1_out, in_1[2]);
  INV6 inv6_1 (
    .I1(in_1[2]), .O1(inv6_1_o1), .GND(1'b0), .VCC(1'b1), .I6(nor4_1_y4), .O6(nor4_1_y3[7]));  // open: I2, O2, I3, O3, I4, O4, I5, O5
  NOR4 nor4_1 (
    .Y1(nor4_1_y3[5]), .B1(inv6_1_o1), .A1(in_1[1]), .Y2(nor4_1_y2), .B2(inv6_1_o1), .A2(in_1[0]),
    .GND(1'b0), .VCC(1'b1), .Y3(nor4_1_y3[4]), .B3(in_1[1]), .A3(in_1[2]), .Y4(nor4_1_y4), .B4(and4_1_y3),
    .A4(and4_1_y1));
  AND4 and4_1 (
    .A1(inv6_1_o1), .B1(in_1[1]), .Y1(and4_1_y1), .A2(nor4_1_y2), .B2(in_1[1]), .Y2(nor4_1_y3[6]),
    .GND(1'b0), .VCC(1'b1), .A3(in_1[1]), .B3(in_1[0]), .Y3(and4_1_y3), .A4(and4_1_y3), .B4(in_1[2]),
    .Y4(nor4_1_y3[8]));
  nor nor_1 (Modptr, in_1[1], in_1[2]);
  nor nor_2 (Jump, in_1[1], not_1_out);
  nor nor_3 (nor_3_out, in_1[0], not_1_out);
  and and_1 (and_1_out, in_1[1], not_1_out);
  and and_2 (and_2_out, in_1[0], in_1[1]);
  and and_3 (WriteOut, nor_3_out, in_1[1]);
  not not_2 (ModMem, nor_4_out);
  nor nor_4 (nor_4_out, and_1_out, and_2_out);
  and and_4 (Hold, and_2_out, in_1[2]);
  assign xnor_1_out = ~({nor4_1_y3, in_1[2], {3{in_1[0]}}} ^ {Hold, ModMem, WriteOut, Jump, Modptr, in_1[2], {3{in_1[0]}}});  // XNOR_Gate xnor_1, 9 bits wide
  and and_5 (and_5_out, xnor_1_out[0], xnor_1_out[1], xnor_1_out[2], xnor_1_out[3], xnor_1_out[4], xnor_1_out[5], xnor_1_out[6], xnor_1_out[7], xnor_1_out[8]);
  // RGBLED rgbled_1: pin names not known; wires that end beside it: rgbled_1_p1, and_5_out
  not not_3 (rgbled_1_p1, and_5_out);

  assign Loopback = in_1[0];
  assign MemOp = in_1[0];
  assign Memsrc = in_1[2];
  assign PtrOp = in_1[0];

  // Notes on the sheet:
  //   PtrOp
  //   MemOp
  //   Loopback
  //   ModMem
  //   Jump
  //   Modptr
  //   MemSrc
  //   Hold
  //   Output
endmodule
