// Logisim project Hold_Logic.circ as structural Verilog: 1 circuit, main circuit main
module main (
  input  Hold,
  input  InVal
);

  wire clock_1_out, d_ff_1_q, d_ff_2_q, multiplexer_1_out, multiplexer_2_out, multiplexer_3_out,
       multiplexer_4_out, not_1_out, not_2_out, or_1_out, t_ff_1_q, t_ff_2_q, undriven, undriven_2,
       undriven_3, undriven_4;

  Clock clock_1 (.out(clock_1_out));
  T_Flip_Flop t_ff_1 (.T(1'b1), .clk(multiplexer_1_out), .Q(t_ff_1_q));  // open: Qn, reset, preset
  Multiplexer #(.enable("false")) multiplexer_1 (
    .in0(undriven), .in1(undriven_2), .out(multiplexer_1_out), .sel(t_ff_1_q));
  D_Flip_Flop d_ff_1 (.D(not_1_out), .clk(multiplexer_2_out), .Q(d_ff_1_q));  // open: Qn, preset, reset
  not not_1 (not_1_out, d_ff_1_q);
  Multiplexer #(.enable("false")) multiplexer_2 (.in0(Hold), .in1(InVal), .out(multiplexer_2_out), .sel(d_ff_1_q));
  D_Flip_Flop d_ff_2 (.D(not_2_out), .clk(multiplexer_3_out), .Q(d_ff_2_q));  // open: Qn, preset, reset
  not not_2 (not_2_out, d_ff_2_q);
  Multiplexer #(.enable("false")) multiplexer_3 (
    .in0(InVal), .in1(clock_1_out), .out(multiplexer_3_out), .sel(d_ff_2_q));
  T_Flip_Flop t_ff_2 (.T(1'b1), .clk(multiplexer_4_out), .Q(t_ff_2_q));  // open: Qn, reset, preset
  Multiplexer #(.enable("false")) multiplexer_4 (
    .in0(undriven_3), .in1(undriven_4), .out(multiplexer_4_out), .sel(t_ff_2_q));
  or or_1 (or_1_out, clock_1_out, d_ff_1_q, d_ff_2_q);

  // Notes on the sheet:
  //   Hold
  //   Input Valid
  //   !Hold State
  //   Clk
  //   Input Valid
  //   !Hold State
endmodule
