// Logisim project PS2_Regs.circ as structural Verilog: 1 circuit, main circuit main
module main (
);

  wire and_1_out, button_1_out, clock_1_out;
  wire [2:0] counter_1_q;

  Button button_1 (.out(button_1_out));
  Clock clock_1 (.out(clock_1_out));
  // Shift_Register shift_register_1: pin names not known
  Counter #(.width(3), .max('h7)) counter_1 (
    .clr(button_1_out), .load(1'b0), .up(1'b1), .count(1'b1), .clk(clock_1_out), .Q(counter_1_q));  // open: D, carry
  and and_1 (and_1_out, counter_1_q[0], counter_1_q[1], counter_1_q[2]);
endmodule
